// Digital circuit clock and program counter.dig as structural Verilog
module clock_and_program_counter (
  input  STEP0,
  input  STEP1,
  input  nCLK_ENABLE,
  input  VCC,
  input  GND,
  input  RD0,
  input  RD1,
  input  RD2,
  input  RD3,
  input  RD4,
  input  RD5,
  input  RD6,
  input  RD7,
  input  A0,
  input  A1,
  input  A2,
  input  A3,
  input  A4,
  input  A5,
  input  A6,
  input  A7,
  input  nRESET,
  input  MS1,
  input  MS0,
  input  AUTO,
  output S_CARRY,
  output Q0,
  output Q1,
  output Q2,
  output Q3,
  output Q4,
  output Q5,
  output Q6,
  output Q7,
  output R_CARRY,
  output RQ0,
  output RQ1,
  output RQ2,
  output RQ3,
  output RQ4,
  output RQ5,
  output RQ6,
  output RQ7,
  output SQ0,
  output SQ1,
  output SQ2,
  output SQ3,
  output SQ4,
  output SQ5,
  output SQ6,
  output SQ7,
  output nRESET_2,
  output CLK,
  output out_54,
  output out_55,
  output RESET
);

  wire _7400_1_pin3, _7400_2_pin3, _7400_2_pin6, _7483real_1_pin13, _7483real_3_pin13, _74173_1_pin3,
       _74173_1_pin4, _74173_1_pin5, BREAK_out, M0, M1, M2, M3, M4, M5, M6, M7, nM_ENABLE, nPC_ENABLE,
       RESET_out, RUN_out, SINGLE_out;

  _7400 _7400_1 (
    .pin1(nRESET_2), .pin2(nCLK_ENABLE), .pin3(_7400_1_pin3), .pin4(_7400_1_pin3), .pin5(_7400_1_pin3),
    .pin6(nPC_ENABLE), .pin7(GND), .pin9(GND), .pin10(GND), .pin11(nM_ENABLE), .pin12(nRESET_2),
    .pin13(nRESET_2), .pin14(VCC));  // open: pin8
  _74153 _74153_1 (
    .pin1(nM_ENABLE), .pin2(MS1), .pin3(GND), .pin4(A6), .pin5(RQ6), .pin6(SQ6), .pin7(M6), .pin8(GND),
    .pin9(M7), .pin10(SQ7), .pin11(RQ7), .pin12(A7), .pin13(GND), .pin14(MS0), .pin15(nM_ENABLE), .pin16(VCC));
  _74153 _74153_2 (
    .pin1(nM_ENABLE), .pin2(MS1), .pin3(GND), .pin4(A4), .pin5(RQ4), .pin6(SQ4), .pin7(M4), .pin8(GND),
    .pin9(M5), .pin10(SQ5), .pin11(RQ5), .pin12(A5), .pin13(GND), .pin14(MS0), .pin15(nM_ENABLE), .pin16(VCC));
  Button SINGLE (.out(SINGLE_out));
  _74153 _74153_3 (
    .pin1(nM_ENABLE), .pin2(MS1), .pin3(GND), .pin4(A2), .pin5(RQ2), .pin6(SQ2), .pin7(M2), .pin8(GND),
    .pin9(M3), .pin10(SQ3), .pin11(RQ3), .pin12(A3), .pin13(GND), .pin14(MS0), .pin15(nM_ENABLE), .pin16(VCC));
  Button #(.activeLow("true")) BREAK (.out(BREAK_out));
  Button #(.activeLow("true")) RUN (.out(RUN_out));
  _74153 _74153_4 (
    .pin1(nM_ENABLE), .pin2(MS1), .pin3(GND), .pin4(A0), .pin5(RQ0), .pin6(SQ0), .pin7(M0), .pin8(GND),
    .pin9(M1), .pin10(SQ1), .pin11(RQ1), .pin12(A1), .pin13(GND), .pin14(MS0), .pin15(nM_ENABLE), .pin16(VCC));
  Button u_RESET (.out(RESET_out));
  PowerSupply powersupply_1 (.VDD(1'b1), .GND(1'b0));
  PowerSupply powersupply_2 (.VDD(1'b1), .GND(1'b0));
  _7483Real _7483real_1 (
    .pin1(Q7), .pin2(RQ6), .pin3(Q6), .pin4(RD6), .pin5(VCC), .pin6(RQ5), .pin7(RD5), .pin8(Q5), .pin9(RQ4),
    .pin10(Q4), .pin11(RD4), .pin12(GND), .pin13(_7483real_1_pin13), .pin14(R_CARRY), .pin15(RQ7), .pin16(RD7));
  Button button_1 ();  // open: out
  _7483Real _7483real_2 (
    .pin1(Q3), .pin2(RQ2), .pin3(Q2), .pin4(RD2), .pin5(VCC), .pin6(RQ1), .pin7(RD1), .pin8(Q1), .pin9(RQ0),
    .pin10(Q0), .pin11(RD0), .pin12(GND), .pin13(GND), .pin14(_7483real_1_pin13), .pin15(RQ3), .pin16(RD3));
  _7400 _7400_2 (
    .pin1(SINGLE_out), .pin2(out_54), .pin3(_7400_2_pin3), .pin4(AUTO), .pin5(out_55), .pin6(_7400_2_pin6),
    .pin7(1'b0), .pin8(out_55), .pin9(RUN_out), .pin10(out_54), .pin11(out_54), .pin12(out_55),
    .pin13(BREAK_out), .pin14(1'b1));
  _7400 _7400_3 (
    .pin1(_7400_2_pin3), .pin2(_7400_2_pin6), .pin3(CLK), .pin4(nRESET_2), .pin5(nRESET_2), .pin6(RESET),
    .pin7(1'b0), .pin9(1'b1), .pin10(1'b1), .pin12(1'b1), .pin13(1'b1), .pin14(1'b1));  // open: pin8, pin11
  _7483Real _7483real_3 (
    .pin1(Q7), .pin2(SQ6), .pin3(Q6), .pin4(GND), .pin5(VCC), .pin6(SQ5), .pin7(GND), .pin8(Q5), .pin9(SQ4),
    .pin10(Q4), .pin11(GND), .pin12(GND), .pin13(_7483real_3_pin13), .pin14(S_CARRY), .pin15(SQ7), .pin16(GND));
  _74377 _74377_1 (
    .pin1(nPC_ENABLE), .pin2(Q0), .pin3(M0), .pin4(M1), .pin5(Q1), .pin6(Q2), .pin7(M2), .pin8(M3),
    .pin9(Q3), .pin10(GND), .pin11(CLK), .pin12(Q4), .pin13(M4), .pin14(M5), .pin15(Q5), .pin16(Q6),
    .pin17(M6), .pin18(M7), .pin19(Q7), .pin20(VCC));
  _74173 _74173_1 (
    .pin1(1'b0), .pin2(1'b0), .pin3(_74173_1_pin3), .pin4(_74173_1_pin4), .pin5(_74173_1_pin5),
    .pin6(nRESET_2), .pin7(CLK), .pin8(1'b0), .pin9(1'b0), .pin10(1'b0), .pin11(_74173_1_pin5),
    .pin12(_74173_1_pin4), .pin13(_74173_1_pin3), .pin14(1'b1), .pin15(RESET_out), .pin16(1'b1));
  _7483Real _7483real_4 (
    .pin1(Q3), .pin2(SQ2), .pin3(Q2), .pin4(GND), .pin5(VCC), .pin6(SQ1), .pin7(STEP1), .pin8(Q1),
    .pin9(SQ0), .pin10(Q0), .pin11(STEP0), .pin12(GND), .pin13(VCC), .pin14(_7483real_3_pin13), .pin15(SQ3),
    .pin16(GND));
  PullDown pulldown_1 (.out(_74173_1_pin3));
  PullDown pulldown_2 (.out(_74173_1_pin4));
  PullDown pulldown_3 (.out(_74173_1_pin5));
  PowerSupply powersupply_3 (.VDD(VCC), .GND(GND));

  // Other names for the same wires on the sheet: nRESET_t = nRESET_2

  // Notes on the sheet:
  //   VCC: default 1
  //   AUTO: Hz: 10
  //   The step counter by default adds 1 to D.
  //   We can increase to a maximum of 4
  //   by setting STEP0 and STEP1.
  //   Relative jumps add RD to D.
  //   For backwards jumps, use
  //   2's compliment arithmetic.
endmodule
