// Digital circuit clock module.dig as structural Verilog
module clock_module (
  input  AUTO,
  output nRESET,
  output CLK,
  output out_4,
  output out_5,
  output RESET
);

  wire _7400_1_pin3, _7400_1_pin6, _74173_1_pin3, _74173_1_pin4, _74173_1_pin5, BREAK_out, RESET_out,
       RUN_out, SINGLE_out;

  Button SINGLE (.out(SINGLE_out));
  Button #(.activeLow("true")) BREAK (.out(BREAK_out));
  Button #(.activeLow("true")) RUN (.out(RUN_out));
  Button u_RESET (.out(RESET_out));
  PowerSupply powersupply_1 (.VDD(1'b1), .GND(1'b0));
  PowerSupply powersupply_2 (.VDD(1'b1), .GND(1'b0));
  _7400 _7400_1 (
    .pin1(SINGLE_out), .pin2(out_4), .pin3(_7400_1_pin3), .pin4(AUTO), .pin5(out_5), .pin6(_7400_1_pin6),
    .pin7(1'b0), .pin8(out_5), .pin9(RUN_out), .pin10(out_4), .pin11(out_4), .pin12(out_5),
    .pin13(BREAK_out), .pin14(1'b1));
  _7400 _7400_2 (
    .pin1(_7400_1_pin3), .pin2(_7400_1_pin6), .pin3(CLK), .pin4(nRESET), .pin5(nRESET), .pin6(RESET),
    .pin7(1'b0), .pin9(1'b1), .pin10(1'b1), .pin12(1'b1), .pin13(1'b1), .pin14(1'b1));  // open: pin8, pin11
  _74173 _74173_1 (
    .pin1(1'b0), .pin2(1'b0), .pin3(_74173_1_pin3), .pin4(_74173_1_pin4), .pin5(_74173_1_pin5),
    .pin6(nRESET), .pin7(CLK), .pin8(1'b0), .pin9(1'b0), .pin10(1'b0), .pin11(_74173_1_pin5),
    .pin12(_74173_1_pin4), .pin13(_74173_1_pin3), .pin14(1'b1), .pin15(RESET_out), .pin16(1'b1));
  PullDown pulldown_1 (.out(_74173_1_pin3));
  PullDown pulldown_2 (.out(_74173_1_pin4));
  PullDown pulldown_3 (.out(_74173_1_pin5));

  // Notes on the sheet:
  //   AUTO: Hz: 10
endmodule
