// Digital circuit clock pc pm rf v21.dig as structural Verilog
module clock_pc_pm_rf_v21 (
  input  STEP0,
  input  STEP1,
  input  nCLK_ENABLE,
  input  W_0,
  input  W_1,
  input  W_2,
  input  W_3,
  input  W_4,
  input  W_5,
  input  W_6,
  input  W_7,
  input  VCC,
  input  GND,
  input  AUTO,
  output S_CARRY,
  output A0,
  output A1,
  output A2,
  output A3,
  output A4,
  output A5,
  output A6,
  output A7,
  output R_CARRY,
  output PM8,
  output PM9,
  output PM10,
  output PM11,
  output PM12,
  output PM13,
  output PM14,
  output PM15,
  output R1_0,
  output R1_1,
  output R1_2,
  output R1_3,
  output R1_4,
  output R1_5,
  output R1_6,
  output R1_7,
  output R2_0,
  output R2_1,
  output R2_2,
  output R2_3,
  output R2_4,
  output R2_5,
  output R2_6,
  output R2_7,
  output R0_2,
  output R1_2_2,
  output RW0,
  output RW1,
  output PM0,
  output PM1,
  output PM2,
  output PM3,
  output PM4,
  output PM5,
  output PM6,
  output PM7,
  output nRESET,
  output CLK,
  output out_63,
  output out_64,
  output RESET
);

  wire _7400_1_pin3, _7400_2_pin3, _7400_2_pin6, _7414_1_pin8, _7483real_1_pin13, _7483real_3_pin13,
       _74173_1_pin3, _74173_1_pin4, _74173_1_pin5, _74377_2_pin2, _74377_2_pin5, _74377_2_pin6,
       _74377_2_pin9, _74377_2_pin12, _74377_2_pin15, _74377_2_pin16, _74377_2_pin19, _74377_3_pin2,
       _74377_3_pin5, _74377_3_pin6, _74377_3_pin9, _74377_3_pin12, _74377_3_pin15, _74377_3_pin16,
       _74377_3_pin19, BTN_BREAK, BTN_RESET, BTN_RUN, BTN_SINGLE, M0, M1, M2, M3, M4, M5, M6, M7, nCLK,
       nM_ENABLE, nPC_ENABLE, nRE0, nRE1, nRE2, nRE3, nWE0, nWE1, RQ0, RQ1, RQ2, RQ3, RQ4, RQ5, RQ6, RQ7,
       SQ0, SQ1, SQ2, SQ3, SQ4, SQ5, SQ6, SQ7;

  PowerSupply powersupply_1 (.VDD(VCC), .GND(GND));
  _74153 _74153_1 (
    .pin1(nM_ENABLE), .pin2(PM1), .pin3(GND), .pin4(W_6), .pin5(RQ6), .pin6(SQ6), .pin7(M6), .pin8(GND),
    .pin9(M7), .pin10(SQ7), .pin11(RQ7), .pin12(W_7), .pin13(GND), .pin14(PM0), .pin15(nM_ENABLE), .pin16(VCC));
  _7400 _7400_1 (
    .pin1(nRESET), .pin2(nCLK_ENABLE), .pin3(_7400_1_pin3), .pin4(_7400_1_pin3), .pin5(_7400_1_pin3),
    .pin6(nPC_ENABLE), .pin7(GND), .pin9(GND), .pin10(GND), .pin11(nM_ENABLE), .pin12(nRESET),
    .pin13(nRESET), .pin14(VCC));  // open: pin8
  _74153 _74153_2 (
    .pin1(nM_ENABLE), .pin2(PM1), .pin3(GND), .pin4(W_4), .pin5(RQ4), .pin6(SQ4), .pin7(M4), .pin8(GND),
    .pin9(M5), .pin10(SQ5), .pin11(RQ5), .pin12(W_5), .pin13(GND), .pin14(PM0), .pin15(nM_ENABLE), .pin16(VCC));
  _74153 _74153_3 (
    .pin1(nM_ENABLE), .pin2(PM1), .pin3(GND), .pin4(W_2), .pin5(RQ2), .pin6(SQ2), .pin7(M2), .pin8(GND),
    .pin9(M3), .pin10(SQ3), .pin11(RQ3), .pin12(W_3), .pin13(GND), .pin14(PM0), .pin15(nM_ENABLE), .pin16(VCC));
  _74153 _74153_4 (
    .pin1(nM_ENABLE), .pin2(PM1), .pin3(GND), .pin4(W_0), .pin5(RQ0), .pin6(SQ0), .pin7(M0), .pin8(GND),
    .pin9(M1), .pin10(SQ1), .pin11(RQ1), .pin12(W_1), .pin13(GND), .pin14(PM0), .pin15(nM_ENABLE), .pin16(VCC));
  Button SINGLE (.out(BTN_SINGLE));
  Button #(.activeLow("true")) BREAK (.out(BTN_BREAK));
  _7483Real _7483real_1 (
    .pin1(A7), .pin2(RQ6), .pin3(A6), .pin4(W_6), .pin5(VCC), .pin6(RQ5), .pin7(W_5), .pin8(A5), .pin9(RQ4),
    .pin10(A4), .pin11(W_4), .pin12(GND), .pin13(_7483real_1_pin13), .pin14(R_CARRY), .pin15(RQ7), .pin16(W_7));
  Button #(.activeLow("true")) RUN (.out(BTN_RUN));
  Button u_RESET (.out(BTN_RESET));
  _7483Real _7483real_2 (
    .pin1(A3), .pin2(RQ2), .pin3(A2), .pin4(W_2), .pin5(VCC), .pin6(RQ1), .pin7(W_1), .pin8(A1), .pin9(RQ0),
    .pin10(A0), .pin11(W_0), .pin12(GND), .pin13(GND), .pin14(_7483real_1_pin13), .pin15(RQ3), .pin16(W_3));
  _7400 _7400_2 (
    .pin1(BTN_SINGLE), .pin2(out_63), .pin3(_7400_2_pin3), .pin4(AUTO), .pin5(out_64), .pin6(_7400_2_pin6),
    .pin7(GND), .pin8(out_64), .pin9(BTN_RUN), .pin10(out_63), .pin11(out_63), .pin12(out_64),
    .pin13(BTN_BREAK), .pin14(VCC));
  _7400 _7400_3 (
    .pin1(_7400_2_pin3), .pin2(_7400_2_pin6), .pin3(CLK), .pin4(nRESET), .pin5(nRESET), .pin6(RESET),
    .pin7(GND), .pin9(VCC), .pin10(VCC), .pin12(VCC), .pin13(VCC), .pin14(VCC));  // open: pin8, pin11
  _7483Real _7483real_3 (
    .pin1(A7), .pin2(SQ6), .pin3(A6), .pin4(GND), .pin5(VCC), .pin6(SQ5), .pin7(GND), .pin8(A5), .pin9(SQ4),
    .pin10(A4), .pin11(GND), .pin12(GND), .pin13(_7483real_3_pin13), .pin14(S_CARRY), .pin15(SQ7), .pin16(GND));
  _74377 _74377_1 (
    .pin1(nPC_ENABLE), .pin2(A0), .pin3(M0), .pin4(M1), .pin5(A1), .pin6(A2), .pin7(M2), .pin8(M3),
    .pin9(A3), .pin10(GND), .pin11(CLK), .pin12(A4), .pin13(M4), .pin14(M5), .pin15(A5), .pin16(A6),
    .pin17(M6), .pin18(M7), .pin19(A7), .pin20(VCC));
  _74173 _74173_1 (
    .pin1(GND), .pin2(GND), .pin3(_74173_1_pin3), .pin4(_74173_1_pin4), .pin5(_74173_1_pin5), .pin6(nRESET),
    .pin7(CLK), .pin8(GND), .pin9(GND), .pin10(GND), .pin11(_74173_1_pin5), .pin12(_74173_1_pin4),
    .pin13(_74173_1_pin3), .pin14(VCC), .pin15(BTN_RESET), .pin16(VCC));
  _7483Real _7483real_4 (
    .pin1(A3), .pin2(SQ2), .pin3(A2), .pin4(GND), .pin5(VCC), .pin6(SQ1), .pin7(STEP1), .pin8(A1),
    .pin9(SQ0), .pin10(A0), .pin11(STEP0), .pin12(GND), .pin13(VCC), .pin14(_7483real_3_pin13), .pin15(SQ3),
    .pin16(GND));
  PullDown pulldown_1 (.out(_74173_1_pin3));
  PullDown pulldown_2 (.out(_74173_1_pin4));
  PullDown pulldown_3 (.out(_74173_1_pin5));
  eeprom eeprom_1 (
    .nCE(GND), .nOE(RESET), .nWE(VCC), .VCC(VCC), .GND(GND), .I_O0(PM0), .I_O1(PM1), .I_O2(PM2), .I_O3(PM3),
    .I_O4(PM4), .I_O5(PM5), .I_O6(PM6), .I_O7(PM7), .A0(CLK), .A1(A1), .A2(A2), .A3(A3), .A4(A4), .A5(A5),
    .A6(A6), .A7(A7), .A8(GND), .A9(GND), .A10(GND), .A11(GND), .A12(GND), .A13(GND), .A14(GND), .A15(GND));
  nand nand_1 (nCLK, CLK, CLK);
  _74377 _74377_2 (
    .pin1(nWE0), .pin2(_74377_2_pin2), .pin3(W_7), .pin4(W_5), .pin5(_74377_2_pin5), .pin6(_74377_2_pin6),
    .pin7(W_3), .pin8(W_1), .pin9(_74377_2_pin9), .pin10(GND), .pin11(CLK), .pin12(_74377_2_pin12),
    .pin13(W_0), .pin14(W_2), .pin15(_74377_2_pin15), .pin16(_74377_2_pin16), .pin17(W_4), .pin18(W_6),
    .pin19(_74377_2_pin19), .pin20(VCC));
  _74377 _74377_3 (
    .pin1(nWE1), .pin2(_74377_3_pin2), .pin3(W_7), .pin4(W_5), .pin5(_74377_3_pin5), .pin6(_74377_3_pin6),
    .pin7(W_3), .pin8(W_1), .pin9(_74377_3_pin9), .pin10(GND), .pin11(CLK), .pin12(_74377_3_pin12),
    .pin13(W_0), .pin14(W_2), .pin15(_74377_3_pin15), .pin16(_74377_3_pin16), .pin17(W_4), .pin18(W_6),
    .pin19(_74377_3_pin19), .pin20(VCC));
  _74273 _74273_1 (
    .pin1(nRESET), .pin2(PM8), .pin3(PM0), .pin4(PM1), .pin5(PM9), .pin6(PM10), .pin7(PM2), .pin8(PM3),
    .pin9(PM11), .pin10(GND), .pin11(nCLK), .pin12(PM12), .pin13(PM4), .pin14(PM5), .pin15(PM13),
    .pin16(PM14), .pin17(PM6), .pin18(PM7), .pin19(PM15), .pin20(VCC));
  _74245 _74245_1 (
    .pin1(VCC), .pin2(_74377_2_pin2), .pin3(_74377_2_pin19), .pin4(_74377_2_pin5), .pin5(_74377_2_pin16),
    .pin6(_74377_2_pin6), .pin7(_74377_2_pin15), .pin8(_74377_2_pin9), .pin9(_74377_2_pin12), .pin10(GND),
    .pin11(R1_0), .pin12(R1_1), .pin13(R1_2), .pin14(R1_3), .pin15(R1_4), .pin16(R1_5), .pin17(R1_6),
    .pin18(R1_7), .pin19(nRE0), .pin20(VCC));
  _74245 _74245_2 (
    .pin1(VCC), .pin2(_74377_3_pin2), .pin3(_74377_3_pin19), .pin4(_74377_3_pin5), .pin5(_74377_3_pin16),
    .pin6(_74377_3_pin6), .pin7(_74377_3_pin15), .pin8(_74377_3_pin9), .pin9(_74377_3_pin12), .pin10(GND),
    .pin11(R1_0), .pin12(R1_1), .pin13(R1_2), .pin14(R1_3), .pin15(R1_4), .pin16(R1_5), .pin17(R1_6),
    .pin18(R1_7), .pin19(nRE1), .pin20(VCC));
  _7414 _7414_1 (
    .pin1(GND), .pin3(GND), .pin5(GND), .pin7(GND), .pin8(_7414_1_pin8), .pin9(PM3), .pin11(GND),
    .pin13(GND), .pin14(VCC));  // open: pin2, pin4, pin6, pin10, pin12
  _74245 _74245_3 (
    .pin1(VCC), .pin2(_74377_2_pin2), .pin3(_74377_2_pin19), .pin4(_74377_2_pin5), .pin5(_74377_2_pin16),
    .pin6(_74377_2_pin6), .pin7(_74377_2_pin15), .pin8(_74377_2_pin9), .pin9(_74377_2_pin12), .pin10(GND),
    .pin11(W_0), .pin12(W_1), .pin13(W_2), .pin14(W_3), .pin15(W_4), .pin16(W_5), .pin17(W_6), .pin18(W_7),
    .pin19(nRE2), .pin20(VCC));
  _74245 _74245_4 (
    .pin1(VCC), .pin2(_74377_3_pin2), .pin3(_74377_3_pin19), .pin4(_74377_3_pin5), .pin5(_74377_3_pin16),
    .pin6(_74377_3_pin6), .pin7(_74377_3_pin15), .pin8(_74377_3_pin9), .pin9(_74377_3_pin12), .pin10(GND),
    .pin11(W_0), .pin12(W_1), .pin13(W_2), .pin14(W_3), .pin15(W_4), .pin16(W_5), .pin17(W_6), .pin18(W_7),
    .pin19(nRE3), .pin20(VCC));
  _74245 _74245_5 (
    .pin1(VCC), .pin2(PM15), .pin3(PM14), .pin4(PM13), .pin5(PM12), .pin6(PM11), .pin7(PM10), .pin8(PM9),
    .pin9(PM8), .pin10(GND), .pin11(W_0), .pin12(W_1), .pin13(W_2), .pin14(W_3), .pin15(W_4), .pin16(W_5),
    .pin17(W_6), .pin18(W_7), .pin19(_7414_1_pin8), .pin20(VCC));
  _74139 _74139_1 (
    .pin1(GND), .pin2(GND), .pin3(GND), .pin8(GND), .pin10(nWE1), .pin11(nWE0), .pin13(PM5), .pin14(PM4),
    .pin15(GND), .pin16(VCC));  // open: pin4, pin5, pin6, pin7, pin9, pin12
  _74139 _74139_2 (
    .pin1(GND), .pin2(PM4), .pin3(PM5), .pin5(nRE0), .pin6(nRE1), .pin8(GND), .pin10(nRE3), .pin11(nRE2),
    .pin13(PM9), .pin14(PM8), .pin15(PM3), .pin16(VCC));  // open: pin4, pin7, pin9, pin12

  assign R0_2 = PM8;
  assign R1_2_2 = PM9;
  assign R2_0 = W_0;
  assign R2_1 = W_1;
  assign R2_2 = W_2;
  assign R2_3 = W_3;
  assign R2_4 = W_4;
  assign R2_5 = W_5;
  assign R2_6 = W_6;
  assign R2_7 = W_7;
  assign RW0 = PM4;
  assign RW1 = PM5;

  // Other names for the same wires on the sheet: CLK_AUTO = AUTO; LED_BREAK = out_63; LED_RUN = out_64; nIE = PM3;
  //   Q0 = A0; Q1 = A1; Q2 = A2; Q3 = A3; Q4 = A4; Q5 = A5; Q6 = A6; Q7 = A7; RD1_0 = R1_0; RD1_1 = R1_1;
  //   RD1_2 = R1_2; RD1_3 = R1_3; RD1_4 = R1_4; RD1_5 = R1_5; RD1_6 = R1_6; RD1_7 = R1_7; RD2_0 = W_0; WD0 = W_0;
  //   RD2_1 = W_1; WD1 = W_1; RD2_2 = W_2; WD2 = W_2; RD2_3 = W_3; WD3 = W_3; RD2_4 = W_4; WD4 = W_4; RD2_5 = W_5;
  //   WD5 = W_5; RD2_6 = W_6; WD6 = W_6; RD2_7 = W_7; WD7 = W_7

  // Notes on the sheet:
  //   STEP0: default 1
  //   VCC: default 1
  //   AUTO: Hz: 10
  //   Relative jumps add RD to D.
  //   For backwards jumps, use
  //   2's compliment arithmetic.
  //   The step counter by default adds 1 to D.
  //   We can increase to a maximum of 4
  //   by setting STEP0 and STEP1.
endmodule
