// Digital circuit clock pc pm rf v23.dig as structural Verilog
module clock_pc_pm_rf_v23 (
  input  STEP0,
  input  STEP1,
  input  nCLK_ENABLE,
  input  AUTO,
  input  VCC,
  input  GND,
  output S_CARRY,
  output A0,
  output A1,
  output A2,
  output A3,
  output A4,
  output A5,
  output A6,
  output A7,
  output R_CARRY,
  output PM8,
  output PM9,
  output PM10,
  output PM11,
  output PM12,
  output PM13,
  output PM14,
  output PM15,
  output R1_0,
  output R1_1,
  output R1_2,
  output R1_3,
  output R1_4,
  output R1_5,
  output R1_6,
  output R1_7,
  output R2_0,
  output R2_1,
  output R2_2,
  output R2_3,
  output R2_4,
  output R2_5,
  output R2_6,
  output R2_7,
  output R0_2,
  output R1_2_2,
  output RW0,
  output RW1,
  output PM0,
  output PM1,
  output PM2,
  output PM3,
  output PM4,
  output PM5,
  output PM6,
  output PM7,
  output nRESET,
  output CLK,
  output out_53,
  output out_54,
  output RESET,
  output W_0,
  output W_1,
  output W_2,
  output W_3,
  output W_4,
  output W_5,
  output W_6,
  output W_7,
  output RS0_0,
  output RS0_1,
  output RS0_2,
  output RS0_3,
  output RS0_4,
  output RS0_5,
  output RS0_6,
  output RS0_7,
  output RS1_0,
  output RS1_1,
  output RS1_2,
  output RS1_3,
  output RS1_4,
  output RS1_5,
  output RS1_6,
  output RS1_7,
  output out_82
);

  wire _7400_1_pin3, _7400_1_pin6, _7400_3_pin3, _7400_3_pin6, _7414_1_pin8, _7483real_1_pin2,
       _7483real_1_pin6, _7483real_1_pin9, _7483real_1_pin13, _7483real_1_pin15, _7483real_2_pin2,
       _7483real_2_pin6, _7483real_2_pin9, _7483real_2_pin15, _7483real_3_pin13, _7483real_4_pin6,
       _7483real_4_pin9, _74153_1_pin1, _74153_1_pin6, _74153_1_pin10, _74153_2_pin6, _74153_2_pin10,
       _74153_3_pin6, _74153_3_pin10, _74173_1_pin3, _74173_1_pin4, _74173_1_pin5, BTN_BREAK, BTN_RESET,
       BTN_RUN, M0, M1, M2, M3, M4, M5, M6, M7, nCLK, nRE0, nRE1, nRE2, nRE3, nWE0, nWE1;

  PowerSupply powersupply_1 (.VDD(VCC), .GND(GND));
  Button SINGLE (.out(out_82));
  Button #(.activeLow("true")) BREAK (.out(BTN_BREAK));
  _74377 _74377_1 (
    .pin1(nWE0), .pin2(RS0_7), .pin3(R2_7), .pin4(R2_5), .pin5(RS0_5), .pin6(RS0_3), .pin7(R2_3),
    .pin8(R2_1), .pin9(RS0_1), .pin10(GND), .pin11(CLK), .pin12(RS0_0), .pin13(R2_0), .pin14(R2_2),
    .pin15(RS0_2), .pin16(RS0_4), .pin17(R2_4), .pin18(R2_6), .pin19(RS0_6), .pin20(VCC));
  _74377 _74377_2 (
    .pin1(nWE1), .pin2(RS1_7), .pin3(R2_7), .pin4(R2_5), .pin5(RS1_5), .pin6(RS1_3), .pin7(R2_3),
    .pin8(R2_1), .pin9(RS1_1), .pin10(GND), .pin11(CLK), .pin12(RS1_0), .pin13(R2_0), .pin14(R2_2),
    .pin15(RS1_2), .pin16(RS1_4), .pin17(R2_4), .pin18(R2_6), .pin19(RS1_6), .pin20(VCC));
  Button #(.activeLow("true")) RUN (.out(BTN_RUN));
  _74139 _74139_1 (
    .pin1(GND), .pin2(GND), .pin3(GND), .pin8(GND), .pin10(nWE1), .pin11(nWE0), .pin13(PM5), .pin14(PM4),
    .pin15(GND), .pin16(VCC));  // open: pin4, pin5, pin6, pin7, pin9, pin12
  Button u_RESET (.out(BTN_RESET));
  _74139 _74139_2 (
    .pin1(GND), .pin2(PM4), .pin3(PM5), .pin5(nRE0), .pin6(nRE1), .pin8(GND), .pin10(nRE3), .pin11(nRE2),
    .pin13(PM9), .pin14(PM8), .pin15(PM3), .pin16(VCC));  // open: pin4, pin7, pin9, pin12
  _74245 _74245_1 (
    .pin1(VCC), .pin2(RS0_7), .pin3(RS0_6), .pin4(RS0_5), .pin5(RS0_4), .pin6(RS0_3), .pin7(RS0_2),
    .pin8(RS0_1), .pin9(RS0_0), .pin10(GND), .pin11(R1_0), .pin12(R1_1), .pin13(R1_2), .pin14(R1_3),
    .pin15(R1_4), .pin16(R1_5), .pin17(R1_6), .pin18(R1_7), .pin19(nRE0), .pin20(VCC));
  _74245 _74245_2 (
    .pin1(VCC), .pin2(RS1_7), .pin3(RS1_6), .pin4(RS1_5), .pin5(RS1_4), .pin6(RS1_3), .pin7(RS1_2),
    .pin8(RS1_1), .pin9(RS1_0), .pin10(GND), .pin11(R1_0), .pin12(R1_1), .pin13(R1_2), .pin14(R1_3),
    .pin15(R1_4), .pin16(R1_5), .pin17(R1_6), .pin18(R1_7), .pin19(nRE1), .pin20(VCC));
  _7414 _7414_1 (
    .pin1(GND), .pin3(GND), .pin5(GND), .pin7(GND), .pin8(_7414_1_pin8), .pin9(PM3), .pin11(GND),
    .pin13(GND), .pin14(VCC));  // open: pin2, pin4, pin6, pin10, pin12
  _74245 _74245_3 (
    .pin1(VCC), .pin2(RS0_7), .pin3(RS0_6), .pin4(RS0_5), .pin5(RS0_4), .pin6(RS0_3), .pin7(RS0_2),
    .pin8(RS0_1), .pin9(RS0_0), .pin10(GND), .pin11(R2_0), .pin12(R2_1), .pin13(R2_2), .pin14(R2_3),
    .pin15(R2_4), .pin16(R2_5), .pin17(R2_6), .pin18(R2_7), .pin19(nRE2), .pin20(VCC));
  _74245 _74245_4 (
    .pin1(VCC), .pin2(RS1_7), .pin3(RS1_6), .pin4(RS1_5), .pin5(RS1_4), .pin6(RS1_3), .pin7(RS1_2),
    .pin8(RS1_1), .pin9(RS1_0), .pin10(GND), .pin11(R2_0), .pin12(R2_1), .pin13(R2_2), .pin14(R2_3),
    .pin15(R2_4), .pin16(R2_5), .pin17(R2_6), .pin18(R2_7), .pin19(nRE3), .pin20(VCC));
  _74245 _74245_5 (
    .pin1(VCC), .pin2(PM15), .pin3(PM14), .pin4(PM13), .pin5(PM12), .pin6(PM11), .pin7(PM10), .pin8(PM9),
    .pin9(PM8), .pin10(GND), .pin11(R2_0), .pin12(R2_1), .pin13(R2_2), .pin14(R2_3), .pin15(R2_4),
    .pin16(R2_5), .pin17(R2_6), .pin18(R2_7), .pin19(_7414_1_pin8), .pin20(VCC));
  _7483Real _7483real_1 (
    .pin1(A7), .pin2(_7483real_1_pin2), .pin3(A6), .pin4(R2_6), .pin5(VCC), .pin6(_7483real_1_pin6),
    .pin7(R2_5), .pin8(A5), .pin9(_7483real_1_pin9), .pin10(A4), .pin11(R2_4), .pin12(GND),
    .pin13(_7483real_1_pin13), .pin14(R_CARRY), .pin15(_7483real_1_pin15), .pin16(R2_7));
  _7400 _7400_1 (
    .pin1(out_82), .pin2(out_53), .pin3(_7400_1_pin3), .pin4(AUTO), .pin5(out_54), .pin6(_7400_1_pin6),
    .pin7(GND), .pin8(out_54), .pin9(BTN_RUN), .pin10(out_53), .pin11(out_53), .pin12(out_54),
    .pin13(BTN_BREAK), .pin14(VCC));
  _74153 _74153_1 (
    .pin1(_74153_1_pin1), .pin2(PM1), .pin3(GND), .pin4(R2_6), .pin5(_7483real_1_pin2), .pin6(_74153_1_pin6),
    .pin7(M6), .pin8(GND), .pin9(M7), .pin10(_74153_1_pin10), .pin11(_7483real_1_pin15), .pin12(R2_7),
    .pin13(GND), .pin14(PM0), .pin15(_74153_1_pin1), .pin16(VCC));
  _7483Real _7483real_2 (
    .pin1(A3), .pin2(_7483real_2_pin2), .pin3(A2), .pin4(R2_2), .pin5(VCC), .pin6(_7483real_2_pin6),
    .pin7(R2_1), .pin8(A1), .pin9(_7483real_2_pin9), .pin10(A0), .pin11(R2_0), .pin12(GND), .pin13(GND),
    .pin14(_7483real_1_pin13), .pin15(_7483real_2_pin15), .pin16(R2_3));
  _7400 _7400_2 (
    .pin1(_7400_1_pin3), .pin2(_7400_1_pin6), .pin3(CLK), .pin4(nRESET), .pin5(nRESET), .pin6(RESET),
    .pin7(GND), .pin9(VCC), .pin10(VCC), .pin12(VCC), .pin13(VCC), .pin14(VCC));  // open: pin8, pin11
  _74153 _74153_2 (
    .pin1(_74153_1_pin1), .pin2(PM1), .pin3(GND), .pin4(R2_4), .pin5(_7483real_1_pin9), .pin6(_74153_2_pin6),
    .pin7(M4), .pin8(GND), .pin9(M5), .pin10(_74153_2_pin10), .pin11(_7483real_1_pin6), .pin12(R2_5),
    .pin13(GND), .pin14(PM0), .pin15(_74153_1_pin1), .pin16(VCC));
  _74173 _74173_1 (
    .pin1(GND), .pin2(GND), .pin3(_74173_1_pin3), .pin4(_74173_1_pin4), .pin5(_74173_1_pin5), .pin6(nRESET),
    .pin7(CLK), .pin8(GND), .pin9(GND), .pin10(GND), .pin11(_74173_1_pin5), .pin12(_74173_1_pin4),
    .pin13(_74173_1_pin3), .pin14(VCC), .pin15(BTN_RESET), .pin16(VCC));
  _7483Real _7483real_3 (
    .pin1(A7), .pin2(_74153_1_pin6), .pin3(A6), .pin4(GND), .pin5(VCC), .pin6(_74153_2_pin10), .pin7(GND),
    .pin8(A5), .pin9(_74153_2_pin6), .pin10(A4), .pin11(GND), .pin12(GND), .pin13(_7483real_3_pin13),
    .pin14(S_CARRY), .pin15(_74153_1_pin10), .pin16(GND));
  _74273 _74273_1 (
    .pin1(nRESET), .pin2(PM8), .pin3(PM0), .pin4(PM1), .pin5(PM9), .pin6(PM10), .pin7(PM2), .pin8(PM3),
    .pin9(PM11), .pin10(GND), .pin11(nCLK), .pin12(PM12), .pin13(PM4), .pin14(PM5), .pin15(PM13),
    .pin16(PM14), .pin17(PM6), .pin18(PM7), .pin19(PM15), .pin20(VCC));
  _74153 _74153_3 (
    .pin1(_74153_1_pin1), .pin2(PM1), .pin3(GND), .pin4(R2_2), .pin5(_7483real_2_pin2), .pin6(_74153_3_pin6),
    .pin7(M2), .pin8(GND), .pin9(M3), .pin10(_74153_3_pin10), .pin11(_7483real_2_pin15), .pin12(R2_3),
    .pin13(GND), .pin14(PM0), .pin15(_74153_1_pin1), .pin16(VCC));
  PullDown pulldown_1 (.out(_74173_1_pin3));
  PullDown pulldown_2 (.out(_74173_1_pin4));
  PullDown pulldown_3 (.out(_74173_1_pin5));
  _7483Real _7483real_4 (
    .pin1(A3), .pin2(_74153_3_pin6), .pin3(A2), .pin4(GND), .pin5(VCC), .pin6(_7483real_4_pin6),
    .pin7(STEP1), .pin8(A1), .pin9(_7483real_4_pin9), .pin10(A0), .pin11(STEP0), .pin12(GND), .pin13(GND),
    .pin14(_7483real_3_pin13), .pin15(_74153_3_pin10), .pin16(GND));
  _74153 _74153_4 (
    .pin1(_74153_1_pin1), .pin2(PM1), .pin3(GND), .pin4(R2_0), .pin5(_7483real_2_pin9),
    .pin6(_7483real_4_pin9), .pin7(M0), .pin8(GND), .pin9(M1), .pin10(_7483real_4_pin6),
    .pin11(_7483real_2_pin6), .pin12(R2_1), .pin13(GND), .pin14(PM0), .pin15(_74153_1_pin1), .pin16(VCC));
  eeprom eeprom_1 (
    .nCE(GND), .nOE(RESET), .nWE(VCC), .VCC(VCC), .GND(GND), .I_O0(PM0), .I_O1(PM1), .I_O2(PM2), .I_O3(PM3),
    .I_O4(PM4), .I_O5(PM5), .I_O6(PM6), .I_O7(PM7), .A0(CLK), .A1(A1), .A2(A2), .A3(A3), .A4(A4), .A5(A5),
    .A6(A6), .A7(A7), .A8(GND), .A9(GND), .A10(GND), .A11(GND), .A12(GND), .A13(GND), .A14(GND), .A15(GND));
  _7400 _7400_3 (
    .pin1(nRESET), .pin2(nCLK_ENABLE), .pin3(_7400_3_pin3), .pin4(_7400_3_pin3), .pin5(_7400_3_pin3),
    .pin6(_7400_3_pin6), .pin7(GND), .pin8(nCLK), .pin9(CLK), .pin10(CLK), .pin11(_74153_1_pin1),
    .pin12(nRESET), .pin13(nRESET), .pin14(VCC));
  _74377 _74377_3 (
    .pin1(_7400_3_pin6), .pin2(A7), .pin3(M7), .pin4(M5), .pin5(A5), .pin6(A3), .pin7(M3), .pin8(M1),
    .pin9(A1), .pin10(GND), .pin11(CLK), .pin12(A0), .pin13(M0), .pin14(M2), .pin15(A2), .pin16(A4),
    .pin17(M4), .pin18(M6), .pin19(A6), .pin20(VCC));

  assign R0_2 = PM8;
  assign R1_2_2 = PM9;
  assign RW0 = PM4;
  assign RW1 = PM5;
  assign W_0 = R2_0;
  assign W_1 = R2_1;
  assign W_2 = R2_2;
  assign W_3 = R2_3;
  assign W_4 = R2_4;
  assign W_5 = R2_5;
  assign W_6 = R2_6;
  assign W_7 = R2_7;

  // Other names for the same wires on the sheet: BTN_SINGLE = out_82; CLK_AUTO = AUTO; LED_BREAK = out_53;
  //   LED_RUN = out_54; nIE = PM3; Q0 = A0; Q1 = A1; Q2 = A2; Q3 = A3; Q4 = A4; Q5 = A5; Q6 = A6; Q7 = A7;
  //   RD1_0 = R1_0; RD1_1 = R1_1; RD1_2 = R1_2; RD1_3 = R1_3; RD1_4 = R1_4; RD1_5 = R1_5; RD1_6 = R1_6; RD1_7 = R1_7;
  //   RD2_0 = R2_0; WD0 = R2_0; RD2_1 = R2_1; WD1 = R2_1; RD2_2 = R2_2; WD2 = R2_2; RD2_3 = R2_3; WD3 = R2_3;
  //   RD2_4 = R2_4; WD4 = R2_4; RD2_5 = R2_5; WD5 = R2_5; RD2_6 = R2_6; WD6 = R2_6; RD2_7 = R2_7; WD7 = R2_7

  // Notes on the sheet:
  //   STEP0: default 1
  //   AUTO: Hz: 20
  //   VCC: default 1
  //   Relative jumps add RD to D.
  //   For backwards jumps, use
  //   2's compliment arithmetic.
  //   The step counter by default adds 1 to D.
  //   We can increase to a maximum of 4
  //   by setting STEP0 and STEP1.
  //   Finish wiring up the clock and program memory.
  //   Maybe move clock controls underneath the clock module.
  //   Then have all the various output leds on top of the clock module.
  //   Not sure about this though.
endmodule
