// Digital circuit program counter v21.dig as structural Verilog
module program_counter_v21 (
  input  VCC,
  input  GND
);

  wire _7400_1_pin3, _7400_1_pin6, _7483real_1_pin2, _7483real_1_pin6, _7483real_1_pin9, _7483real_1_pin13,
       _7483real_1_pin15, _7483real_2_pin2, _7483real_2_pin6, _7483real_2_pin9, _7483real_2_pin15,
       _7483real_3_pin13, _7483real_4_pin6, _7483real_4_pin9, _74153_1_pin6, _74153_1_pin10, _74153_2_pin6,
       _74153_2_pin10, _74153_3_pin6, _74153_3_pin10, CLK, M0, M1, M2, M3, M4, M5, M6, M7, nCLK_ENABLE,
       nM_ENABLE, nRESET, PM0, PM1, Q0, Q1, Q2, Q3, Q4, Q5, Q6, Q7, RD2_0, RD2_1, RD2_2, RD2_3, RD2_4, RD2_5,
       RD2_6, RD2_7, STEP0, STEP1;

  PowerSupply powersupply_1 (.VDD(VCC), .GND(GND));
  _7483Real _7483real_1 (
    .pin1(Q7), .pin2(_7483real_1_pin2), .pin3(Q6), .pin4(RD2_6), .pin5(VCC), .pin6(_7483real_1_pin6),
    .pin7(RD2_5), .pin8(Q5), .pin9(_7483real_1_pin9), .pin10(Q4), .pin11(RD2_4), .pin12(GND),
    .pin13(_7483real_1_pin13), .pin15(_7483real_1_pin15), .pin16(RD2_7));  // open: pin14
  _74153 _74153_1 (
    .pin1(nM_ENABLE), .pin2(PM1), .pin3(GND), .pin4(RD2_6), .pin5(_7483real_1_pin2), .pin6(_74153_1_pin6),
    .pin7(M6), .pin8(GND), .pin9(M7), .pin10(_74153_1_pin10), .pin11(_7483real_1_pin15), .pin12(RD2_7),
    .pin13(GND), .pin14(PM0), .pin15(nM_ENABLE), .pin16(VCC));
  _7483Real _7483real_2 (
    .pin1(Q3), .pin2(_7483real_2_pin2), .pin3(Q2), .pin4(RD2_2), .pin5(VCC), .pin6(_7483real_2_pin6),
    .pin7(RD2_1), .pin8(Q1), .pin9(_7483real_2_pin9), .pin10(Q0), .pin11(RD2_0), .pin12(GND), .pin13(GND),
    .pin14(_7483real_1_pin13), .pin15(_7483real_2_pin15), .pin16(RD2_3));
  _74153 _74153_2 (
    .pin1(nM_ENABLE), .pin2(PM1), .pin3(GND), .pin4(RD2_4), .pin5(_7483real_1_pin9), .pin6(_74153_2_pin6),
    .pin7(M4), .pin8(GND), .pin9(M5), .pin10(_74153_2_pin10), .pin11(_7483real_1_pin6), .pin12(RD2_5),
    .pin13(GND), .pin14(PM0), .pin15(nM_ENABLE), .pin16(VCC));
  _7483Real _7483real_3 (
    .pin1(Q7), .pin2(_74153_1_pin6), .pin3(Q6), .pin4(GND), .pin5(VCC), .pin6(_74153_2_pin10), .pin7(GND),
    .pin8(Q5), .pin9(_74153_2_pin6), .pin10(Q4), .pin11(GND), .pin12(GND), .pin13(_7483real_3_pin13),
    .pin15(_74153_1_pin10), .pin16(GND));  // open: pin14
  _74153 _74153_3 (
    .pin1(nM_ENABLE), .pin2(PM1), .pin3(GND), .pin4(RD2_2), .pin5(_7483real_2_pin2), .pin6(_74153_3_pin6),
    .pin7(M2), .pin8(GND), .pin9(M3), .pin10(_74153_3_pin10), .pin11(_7483real_2_pin15), .pin12(RD2_3),
    .pin13(GND), .pin14(PM0), .pin15(nM_ENABLE), .pin16(VCC));
  _7483Real _7483real_4 (
    .pin1(Q3), .pin2(_74153_3_pin6), .pin3(Q2), .pin4(GND), .pin5(VCC), .pin6(_7483real_4_pin6),
    .pin7(STEP1), .pin8(Q1), .pin9(_7483real_4_pin9), .pin10(Q0), .pin11(STEP0), .pin12(GND), .pin13(GND),
    .pin14(_7483real_3_pin13), .pin15(_74153_3_pin10), .pin16(GND));
  _74153 _74153_4 (
    .pin1(nM_ENABLE), .pin2(PM1), .pin3(GND), .pin4(RD2_0), .pin5(_7483real_2_pin9), .pin6(_7483real_4_pin9),
    .pin7(M0), .pin8(GND), .pin9(M1), .pin10(_7483real_4_pin6), .pin11(_7483real_2_pin6), .pin12(RD2_1),
    .pin13(GND), .pin14(PM0), .pin15(nM_ENABLE), .pin16(VCC));
  _7400 _7400_1 (
    .pin1(nRESET), .pin2(nCLK_ENABLE), .pin3(_7400_1_pin3), .pin4(_7400_1_pin3), .pin5(_7400_1_pin3),
    .pin6(_7400_1_pin6), .pin7(GND), .pin9(GND), .pin10(GND), .pin11(nM_ENABLE), .pin12(nRESET),
    .pin13(nRESET), .pin14(VCC));  // open: pin8
  _74377 _74377_1 (
    .pin1(_7400_1_pin6), .pin2(Q7), .pin3(M7), .pin4(M5), .pin5(Q5), .pin6(Q3), .pin7(M3), .pin8(M1),
    .pin9(Q1), .pin10(GND), .pin11(CLK), .pin12(Q0), .pin13(M0), .pin14(M2), .pin15(Q2), .pin16(Q4),
    .pin17(M4), .pin18(M6), .pin19(Q6), .pin20(VCC));

  // Notes on the sheet:
  //   VCC: default 1
endmodule
