// Digital circuit program memory.dig as structural Verilog
module program_memory (
  input  VCC,
  input  GND,
  input  A0,
  input  A1,
  input  A2,
  input  A3,
  input  A4,
  input  A5,
  input  A6,
  input  A7,
  input  in_27,
  output D0,
  output D1,
  output D2,
  output D3,
  output D4,
  output D5,
  output D6,
  output D7,
  output D8,
  output D9,
  output D10,
  output D11,
  output D12,
  output D13,
  output D14,
  output D15
);

  wire nCLK;

  eeprom eeprom_1 (
    .nCE(GND), .nOE(GND), .nWE(VCC), .VCC(VCC), .GND(GND), .I_O0(D0), .I_O1(D1), .I_O2(D2), .I_O3(D3),
    .I_O4(D4), .I_O5(D5), .I_O6(D6), .I_O7(D7), .A0(in_27), .A1(A1), .A2(A2), .A3(A3), .A4(A4), .A5(A5),
    .A6(A6), .A7(A7), .A8(GND), .A9(GND), .A10(GND), .A11(GND), .A12(GND), .A13(GND), .A14(GND), .A15(GND));
  nand nand_1 (nCLK, in_27, in_27);
  PowerSupply powersupply_1 (.VDD(VCC), .GND(GND));
  _74273 _74273_1 (
    .pin1(VCC), .pin2(D8), .pin3(D0), .pin4(D1), .pin5(D9), .pin6(D10), .pin7(D2), .pin8(D3), .pin9(D11),
    .pin10(GND), .pin11(nCLK), .pin12(D12), .pin13(D4), .pin14(D5), .pin15(D13), .pin16(D14), .pin17(D6),
    .pin18(D7), .pin19(D15), .pin20(VCC));

  // Other names for the same wires on the sheet: CLK = in_27

  // Notes on the sheet:
  //   VCC: default 1
endmodule
