// Digital circuit register file 8x16.dig as structural Verilog
module register_file_8x16 (
  input  VCC,
  input  GND
);

  wire _74245_6_pin2, _74245_6_pin3, _74245_6_pin4, _74245_6_pin5, _74245_6_pin6, _74245_6_pin7,
       _74245_6_pin8, _74245_6_pin9, _74245_6_pin10, _74245_8_pin2, _74245_8_pin3, _74245_8_pin4,
       _74245_8_pin5, _74245_8_pin6, _74245_8_pin7, _74245_8_pin8, _74245_8_pin9, _74245_8_pin10,
       _74245_8_pin20, _74377_1_pin2, _74377_1_pin5, _74377_1_pin6, _74377_1_pin12, _74377_1_pin15,
       _74377_1_pin16, _74377_1_pin19, _74377_2_pin2, _74377_2_pin5, _74377_2_pin6, _74377_2_pin12,
       _74377_2_pin15, _74377_2_pin16, _74377_2_pin19, _74377_3_pin2, _74377_3_pin3, _74377_3_pin4,
       _74377_3_pin5, _74377_3_pin6, _74377_3_pin7, _74377_3_pin8, _74377_3_pin9, _74377_3_pin12,
       _74377_3_pin13, _74377_3_pin14, _74377_3_pin15, _74377_3_pin16, _74377_3_pin17, _74377_3_pin18,
       _74377_3_pin19, _74377_4_pin2, _74377_4_pin3, _74377_4_pin4, _74377_4_pin5, _74377_4_pin6,
       _74377_4_pin7, _74377_4_pin8, _74377_4_pin9, _74377_4_pin10, _74377_4_pin12, _74377_4_pin13,
       _74377_4_pin14, _74377_4_pin15, _74377_4_pin16, _74377_4_pin17, _74377_4_pin18, _74377_4_pin19,
       _74377_4_pin20, A0, A1, A2, A3, A4, A5, A6, A7, B0, B1, B2, B3, B4, B5, B6, B7, CLK, D0, D1, D2, D3,
       D4, D5, D6, D7;

  // _74154 _74154_1: pin names not known
  PowerSupply powersupply_1 (.VDD(VCC), .GND(GND));
  _74377 _74377_1 (
    .pin2(_74377_1_pin2), .pin3(D6), .pin4(D4), .pin5(_74377_1_pin5), .pin6(_74377_1_pin6), .pin7(D2),
    .pin8(D0), .pin9(VCC), .pin10(GND), .pin11(CLK), .pin12(_74377_1_pin12), .pin13(D1), .pin14(D3),
    .pin15(_74377_1_pin15), .pin16(_74377_1_pin16), .pin17(D5), .pin18(D7), .pin19(_74377_1_pin19),
    .pin20(VCC));  // open: pin1
  _74377 _74377_2 (
    .pin2(_74377_2_pin2), .pin3(D6), .pin4(D4), .pin5(_74377_2_pin5), .pin6(_74377_2_pin6), .pin7(D2),
    .pin8(D0), .pin9(VCC), .pin10(GND), .pin11(CLK), .pin12(_74377_2_pin12), .pin13(D1), .pin14(D3),
    .pin15(_74377_2_pin15), .pin16(_74377_2_pin16), .pin17(D5), .pin18(D7), .pin19(_74377_2_pin19),
    .pin20(VCC));  // open: pin1
  _74245 _74245_1 (
    .pin1(GND), .pin2(A7), .pin3(A6), .pin4(A5), .pin5(A4), .pin6(A3), .pin7(A2), .pin8(A1), .pin9(A0),
    .pin10(GND), .pin11(VCC), .pin12(_74377_1_pin12), .pin13(_74377_1_pin6), .pin14(_74377_1_pin15),
    .pin15(_74377_1_pin5), .pin16(_74377_1_pin16), .pin17(_74377_1_pin2), .pin18(_74377_1_pin19));  // open: pin19, pin20
  _74245 _74245_2 (
    .pin1(GND), .pin2(A7), .pin3(A6), .pin4(A5), .pin5(A4), .pin6(A3), .pin7(A2), .pin8(A1), .pin9(A0),
    .pin10(GND), .pin11(VCC), .pin12(_74377_2_pin12), .pin13(_74377_2_pin6), .pin14(_74377_2_pin15),
    .pin15(_74377_2_pin5), .pin16(_74377_2_pin16), .pin17(_74377_2_pin2), .pin18(_74377_2_pin19), .pin20(VCC));  // open: pin19
  _74245 _74245_3 (
    .pin1(GND), .pin2(B7), .pin3(B6), .pin4(B5), .pin5(B4), .pin6(B3), .pin7(B2), .pin8(B1), .pin9(B0),
    .pin10(GND), .pin11(VCC), .pin12(_74377_1_pin12), .pin13(_74377_1_pin6), .pin14(_74377_1_pin15),
    .pin15(_74377_1_pin5), .pin16(_74377_1_pin16), .pin17(_74377_1_pin2), .pin18(_74377_1_pin19), .pin20(VCC));  // open: pin19
  _74245 _74245_4 (
    .pin1(GND), .pin2(B7), .pin3(B6), .pin4(B5), .pin5(B4), .pin6(B3), .pin7(B2), .pin8(B1), .pin9(B0),
    .pin10(GND), .pin11(VCC), .pin12(_74377_2_pin12), .pin13(_74377_2_pin6), .pin14(_74377_2_pin15),
    .pin15(_74377_2_pin5), .pin16(_74377_2_pin16), .pin17(_74377_2_pin2), .pin18(_74377_2_pin19), .pin20(VCC));  // open: pin19
  _74377 _74377_3 (
    .pin2(_74377_3_pin2), .pin3(_74377_3_pin3), .pin4(_74377_3_pin4), .pin5(_74377_3_pin5),
    .pin6(_74377_3_pin6), .pin7(_74377_3_pin7), .pin8(_74377_3_pin8), .pin9(_74377_3_pin9),
    .pin12(_74377_3_pin12), .pin13(_74377_3_pin13), .pin14(_74377_3_pin14), .pin15(_74377_3_pin15),
    .pin16(_74377_3_pin16), .pin17(_74377_3_pin17), .pin18(_74377_3_pin18), .pin19(_74377_3_pin19));  // open: pin1, pin10, pin11, pin20
  _74377 _74377_4 (
    .pin2(_74377_4_pin2), .pin3(_74377_4_pin3), .pin4(_74377_4_pin4), .pin5(_74377_4_pin5),
    .pin6(_74377_4_pin6), .pin7(_74377_4_pin7), .pin8(_74377_4_pin8), .pin9(_74377_4_pin9),
    .pin10(_74377_4_pin10), .pin11(CLK), .pin12(_74377_4_pin12), .pin13(_74377_4_pin13),
    .pin14(_74377_4_pin14), .pin15(_74377_4_pin15), .pin16(_74377_4_pin16), .pin17(_74377_4_pin17),
    .pin18(_74377_4_pin18), .pin19(_74377_4_pin19), .pin20(_74377_4_pin20));  // open: pin1
  _74245 _74245_5 (
    .pin11(_74377_3_pin9), .pin12(_74377_3_pin12), .pin13(_74377_3_pin6), .pin14(_74377_3_pin15),
    .pin15(_74377_3_pin5), .pin16(_74377_3_pin16), .pin17(_74377_3_pin2), .pin18(_74377_3_pin19));  // open: pin1, pin2, pin3, pin4, pin5, pin6, pin7, pin8, pin9, pin10, pin19, pin20
  _74245 _74245_6 (
    .pin1(_74377_4_pin10), .pin2(_74245_6_pin2), .pin3(_74245_6_pin3), .pin4(_74245_6_pin4),
    .pin5(_74245_6_pin5), .pin6(_74245_6_pin6), .pin7(_74245_6_pin7), .pin8(_74245_6_pin8),
    .pin9(_74245_6_pin9), .pin10(_74245_6_pin10), .pin11(_74377_4_pin9), .pin12(_74377_4_pin12),
    .pin13(_74377_4_pin6), .pin14(_74377_4_pin15), .pin15(_74377_4_pin5), .pin16(_74377_4_pin16),
    .pin17(_74377_4_pin2), .pin18(_74377_4_pin19), .pin20(_74377_4_pin9));  // open: pin19
  _74245 _74245_7 (
    .pin11(_74377_3_pin9), .pin12(_74377_3_pin12), .pin13(_74377_3_pin6), .pin14(_74377_3_pin15),
    .pin15(_74377_3_pin5), .pin16(_74377_3_pin16), .pin17(_74377_3_pin2), .pin18(_74377_3_pin19));  // open: pin1, pin2, pin3, pin4, pin5, pin6, pin7, pin8, pin9, pin10, pin19, pin20
  _74245 _74245_8 (
    .pin1(_74245_6_pin10), .pin2(_74245_8_pin2), .pin3(_74245_8_pin3), .pin4(_74245_8_pin4),
    .pin5(_74245_8_pin5), .pin6(_74245_8_pin6), .pin7(_74245_8_pin7), .pin8(_74245_8_pin8),
    .pin9(_74245_8_pin9), .pin10(_74245_8_pin10), .pin11(_74377_4_pin9), .pin12(_74377_4_pin12),
    .pin13(_74377_4_pin6), .pin14(_74377_4_pin15), .pin15(_74377_4_pin5), .pin16(_74377_4_pin16),
    .pin17(_74377_4_pin2), .pin18(_74377_4_pin19), .pin20(_74245_8_pin20));  // open: pin19

  // Notes on the sheet:
  //   VCC: default 1
endmodule
