// Digital circuit register file v2.dig as structural Verilog
module register_file_v2 (
  input  VCC,
  input  GND,
  input  W_0,
  input  W_1,
  input  W_2,
  input  W_3,
  input  W_4,
  input  W_5,
  input  W_6,
  input  W_7,
  input  W0,
  input  W1,
  input  R0_1,
  input  R1_1_2,
  input  R0_2,
  input  R1_2_2,
  input  CLK,
  input  ID_0,
  input  ID_1,
  input  ID_2,
  input  ID_3,
  input  ID_4,
  input  ID_5,
  input  ID_6,
  input  ID_7,
  input  IE,
  output R1_0,
  output R1_1,
  output R1_2,
  output R1_3,
  output R1_4,
  output R1_5,
  output R1_6,
  output R1_7,
  output R2_0,
  output R2_1,
  output R2_2,
  output R2_3,
  output R2_4,
  output R2_5,
  output R2_6,
  output R2_7
);

  wire _7414_1_pin8, _74377_1_pin2, _74377_1_pin5, _74377_1_pin6, _74377_1_pin9, _74377_1_pin12,
       _74377_1_pin15, _74377_1_pin16, _74377_1_pin19, _74377_2_pin2, _74377_2_pin5, _74377_2_pin6,
       _74377_2_pin9, _74377_2_pin12, _74377_2_pin15, _74377_2_pin16, _74377_2_pin19, nRE0, nRE1, nRE2, nRE3,
       nWE0, nWE1;

  _74377 _74377_1 (
    .pin1(nWE0), .pin2(_74377_1_pin2), .pin3(W_7), .pin4(W_5), .pin5(_74377_1_pin5), .pin6(_74377_1_pin6),
    .pin7(W_3), .pin8(W_1), .pin9(_74377_1_pin9), .pin10(GND), .pin11(CLK), .pin12(_74377_1_pin12),
    .pin13(W_0), .pin14(W_2), .pin15(_74377_1_pin15), .pin16(_74377_1_pin16), .pin17(W_4), .pin18(W_6),
    .pin19(_74377_1_pin19), .pin20(VCC));
  _74377 _74377_2 (
    .pin1(nWE1), .pin2(_74377_2_pin2), .pin3(W_7), .pin4(W_5), .pin5(_74377_2_pin5), .pin6(_74377_2_pin6),
    .pin7(W_3), .pin8(W_1), .pin9(_74377_2_pin9), .pin10(GND), .pin11(CLK), .pin12(_74377_2_pin12),
    .pin13(W_0), .pin14(W_2), .pin15(_74377_2_pin15), .pin16(_74377_2_pin16), .pin17(W_4), .pin18(W_6),
    .pin19(_74377_2_pin19), .pin20(VCC));
  _74245 _74245_1 (
    .pin1(VCC), .pin2(_74377_1_pin2), .pin3(_74377_1_pin19), .pin4(_74377_1_pin5), .pin5(_74377_1_pin16),
    .pin6(_74377_1_pin6), .pin7(_74377_1_pin15), .pin8(_74377_1_pin9), .pin9(_74377_1_pin12), .pin10(GND),
    .pin11(R1_0), .pin12(R1_1), .pin13(R1_2), .pin14(R1_3), .pin15(R1_4), .pin16(R1_5), .pin17(R1_6),
    .pin18(R1_7), .pin19(nRE0), .pin20(VCC));
  _74245 _74245_2 (
    .pin1(VCC), .pin2(_74377_2_pin2), .pin3(_74377_2_pin19), .pin4(_74377_2_pin5), .pin5(_74377_2_pin16),
    .pin6(_74377_2_pin6), .pin7(_74377_2_pin15), .pin8(_74377_2_pin9), .pin9(_74377_2_pin12), .pin10(GND),
    .pin11(R1_0), .pin12(R1_1), .pin13(R1_2), .pin14(R1_3), .pin15(R1_4), .pin16(R1_5), .pin17(R1_6),
    .pin18(R1_7), .pin19(nRE1), .pin20(VCC));
  _7414 _7414_1 (
    .pin1(GND), .pin3(GND), .pin5(GND), .pin7(GND), .pin8(_7414_1_pin8), .pin9(IE), .pin11(GND), .pin13(GND),
    .pin14(VCC));  // open: pin2, pin4, pin6, pin10, pin12
  _74245 _74245_3 (
    .pin1(VCC), .pin2(_74377_1_pin2), .pin3(_74377_1_pin19), .pin4(_74377_1_pin5), .pin5(_74377_1_pin16),
    .pin6(_74377_1_pin6), .pin7(_74377_1_pin15), .pin8(_74377_1_pin9), .pin9(_74377_1_pin12), .pin10(GND),
    .pin11(W_0), .pin12(W_1), .pin13(W_2), .pin14(W_3), .pin15(W_4), .pin16(W_5), .pin17(W_6), .pin18(W_7),
    .pin19(nRE2), .pin20(VCC));
  _74245 _74245_4 (
    .pin1(VCC), .pin2(_74377_2_pin2), .pin3(_74377_2_pin19), .pin4(_74377_2_pin5), .pin5(_74377_2_pin16),
    .pin6(_74377_2_pin6), .pin7(_74377_2_pin15), .pin8(_74377_2_pin9), .pin9(_74377_2_pin12), .pin10(GND),
    .pin11(W_0), .pin12(W_1), .pin13(W_2), .pin14(W_3), .pin15(W_4), .pin16(W_5), .pin17(W_6), .pin18(W_7),
    .pin19(nRE3), .pin20(VCC));
  _74245 _74245_5 (
    .pin1(VCC), .pin2(ID_7), .pin3(ID_6), .pin4(ID_5), .pin5(ID_4), .pin6(ID_3), .pin7(ID_2), .pin8(ID_1),
    .pin9(ID_0), .pin10(GND), .pin11(W_0), .pin12(W_1), .pin13(W_2), .pin14(W_3), .pin15(W_4), .pin16(W_5),
    .pin17(W_6), .pin18(W_7), .pin19(_7414_1_pin8), .pin20(VCC));
  PowerSupply powersupply_1 (.VDD(VCC), .GND(GND));
  _74139 _74139_1 (
    .pin1(GND), .pin2(GND), .pin3(GND), .pin8(GND), .pin10(nWE1), .pin11(nWE0), .pin13(W1), .pin14(W0),
    .pin15(GND), .pin16(VCC));  // open: pin4, pin5, pin6, pin7, pin9, pin12
  _74139 _74139_2 (
    .pin1(GND), .pin2(R0_1), .pin3(R1_1_2), .pin5(nRE0), .pin6(nRE1), .pin8(GND), .pin10(nRE3), .pin11(nRE2),
    .pin13(R1_2_2), .pin14(R0_2), .pin15(IE), .pin16(VCC));  // open: pin4, pin7, pin9, pin12

  assign R2_0 = W_0;
  assign R2_1 = W_1;
  assign R2_2 = W_2;
  assign R2_3 = W_3;
  assign R2_4 = W_4;
  assign R2_5 = W_5;
  assign R2_6 = W_6;
  assign R2_7 = W_7;

  // Other names for the same wires on the sheet: nIE = IE; R0 = R0_1; R1 = R1_1_2; R2 = R0_2; R3 = R1_2_2;
  //   RD1_0 = R1_0; RD1_1 = R1_1; RD1_2 = R1_2; RD1_3 = R1_3; RD1_4 = R1_4; RD1_5 = R1_5; RD1_6 = R1_6; RD1_7 = R1_7;
  //   RD2_0 = W_0; WD0 = W_0; RD2_1 = W_1; WD1 = W_1; RD2_2 = W_2; WD2 = W_2; RD2_3 = W_3; WD3 = W_3; RD2_4 = W_4;
  //   WD4 = W_4; RD2_5 = W_5; WD5 = W_5; RD2_6 = W_6; WD6 = W_6; RD2_7 = W_7; WD7 = W_7

  // Notes on the sheet:
  //   VCC: default 1
endmodule
