// Digital circuit clock.dig as structural Verilog
module clock (
  input  CLK_AUTO,
  input  BTN_SINGLE,
  input  BTN_BREAK,
  input  BTN_RUN,
  input  BTN_RESET,
  output LED_BREAK,
  output LED_RUN,
  output RESET,
  output nRESET,
  output CLK
);

  wire _7400_1_pin3, _7400_1_pin6, _74173_1_pin3, _74173_1_pin4, _74173_1_pin5;

  PowerSupply powersupply_1 (.VDD(1'b1), .GND(1'b0));
  _7400 _7400_1 (
    .pin1(BTN_SINGLE), .pin2(LED_BREAK), .pin3(_7400_1_pin3), .pin4(CLK_AUTO), .pin5(LED_RUN),
    .pin6(_7400_1_pin6), .pin7(1'b0), .pin8(LED_RUN), .pin9(BTN_RUN), .pin10(LED_BREAK), .pin11(LED_BREAK),
    .pin12(LED_RUN), .pin13(BTN_BREAK), .pin14(1'b1));
  _7400 _7400_2 (
    .pin1(_7400_1_pin3), .pin2(_7400_1_pin6), .pin3(CLK), .pin4(nRESET), .pin5(nRESET), .pin6(RESET),
    .pin7(1'b0), .pin9(1'b1), .pin10(1'b1), .pin12(1'b1), .pin13(1'b1), .pin14(1'b1));  // open: pin8, pin11
  _74173 _74173_1 (
    .pin1(1'b0), .pin2(1'b0), .pin3(_74173_1_pin3), .pin4(_74173_1_pin4), .pin5(_74173_1_pin5),
    .pin6(nRESET), .pin7(CLK), .pin8(1'b0), .pin9(1'b0), .pin10(1'b0), .pin11(_74173_1_pin5),
    .pin12(_74173_1_pin4), .pin13(_74173_1_pin3), .pin14(1'b1), .pin15(BTN_RESET), .pin16(1'b1));
  PullDown pulldown_1 (.out(_74173_1_pin3));
  PullDown pulldown_2 (.out(_74173_1_pin4));
  PullDown pulldown_3 (.out(_74173_1_pin5));

  // Notes on the sheet:
  //   BTN_BREAK: default 1
  //   BTN_RUN: default 1
endmodule
