// Digital circuit eeprom.dig as structural Verilog
// 512K-Bit (64K x 8) CMOS Parallel EEPROM;
// DATA Polling for End of Write Detection not implemented!
module eeprom (
  input  nCE,
  input  nOE,
  input  nWE,
  input  VCC,
  input  GND,
  input  I_O0,
  input  I_O1,
  input  I_O2,
  input  I_O3,
  input  I_O4,
  input  I_O5,
  input  I_O6,
  input  I_O7,
  input  A0,
  input  A1,
  input  A2,
  input  A3,
  input  A4,
  input  A5,
  input  A6,
  input  A7,
  input  A8,
  input  A9,
  input  A10,
  input  A11,
  input  A12,
  input  A13,
  input  A14,
  input  A15
);

  wire nor_1_out;
  wire [7:0] eeprom_d;

  EEPROM #(.AddrBits(16), .Bits(8)) eeprom (
    .A({A15, A14, A13, A12, A11, A10, A9, A8, A7, A6, A5, A4, A3, A2, A1, A0}), .CS(~nCE), .WE(~nWE),
    .OE(~nOE), .D(eeprom_d));
  nor nor_1 (nor_1_out, nCE, ~nWE, nOE);  // NOr
  PowerSupply powersupply_1 (.VDD(VCC), .GND(GND));
  BusSplitter #(.Bits(8)) bussplitter_1 (
    .D(eeprom_d), .OE(nor_1_out), .D0(I_O0), .D1(I_O1), .D2(I_O2), .D3(I_O3), .D4(I_O4), .D5(I_O5),
    .D6(I_O6), .D7(I_O7));

  // Notes on the sheet:
  //   nCE: pin 22, default 1
  //   nOE: pin 24, default 1
  //   nWE: pin 31, default 1
  //   VCC: pin 32, default 1
  //   GND: pin 16
  //   I_O0: pin 13
  //   I_O1: pin 14
  //   I_O2: pin 15
  //   I_O3: pin 17
  //   I_O4: pin 18
  //   I_O5: pin 19
  //   I_O6: pin 20
  //   I_O7: pin 21
  //   A0: pin 12
  //   A1: pin 11
  //   A2: pin 10
  //   A3: pin 9
  //   A4: pin 8
  //   A5: pin 7
  //   A6: pin 6
  //   A7: pin 5
  //   A8: pin 27
  //   A9: pin 26
  //   A10: pin 23
  //   A11: pin 25
  //   A12: pin 4
  //   A13: pin 28
  //   A14: pin 29
  //   A15: pin 3
  //   contents of eeprom (hex, n*v repeats v):
  //   18,0,20,1,30,2,40,3,50,4,60,5,70,6,9,12,16*0,18,f0,28,55,38,aa
  //   ,48,f,58,81,68,42,78,ff,18,6,1,1,4*0,18,40,28,f0,2,1,9,61443*0
  //   ,18,1,28,2,38,4,48,8,58,10,68,20,78,40,0,0,18,80,28,40,38,20,48
  //   ,10,58,8,68,4,78,2,0,0,9,e0
endmodule
