// Digital circuit program counter.dig as structural Verilog
module program_counter (
  input  [7:0] RB,
  input  nCLK_ENABLE,
  input  CLK,
  input  RESET,
  input  nRESET,
  input  STEP_1,
  input  STEP_0,
  input  MODE_1,
  input  MODE_0,
  output nCLK,
  output [7:0] A0,
  output REL_CARRY,
  output STEP_CARRY
);

  wire _7400_1_pin3, _7483real_1_pin13, _7483real_2_pin13, M0, M1, M2, M3, M4, M5, M6, M7, nR_ENABLE, REL_0,
       REL_1, REL_2, REL_3, REL_4, REL_5, REL_6, REL_7, STEP_0_t, STEP_1_t, STEP_2, STEP_3, STEP_4, STEP_5,
       STEP_6, STEP_7;

  PowerSupply powersupply_1 (.VDD(1'b1), .GND(1'b0));
  _7400 _7400_1 (
    .pin1(nCLK_ENABLE), .pin2(nRESET), .pin3(_7400_1_pin3), .pin4(_7400_1_pin3), .pin5(_7400_1_pin3),
    .pin6(nR_ENABLE), .pin7(1'b0), .pin8(nCLK), .pin9(CLK), .pin10(CLK), .pin12(1'b1), .pin13(1'b1),
    .pin14(1'b1));  // open: pin11
  _74153 _74153_1 (
    .pin1(RESET), .pin2(MODE_1), .pin3(1'b0), .pin4(RB[6]), .pin5(REL_6), .pin6(STEP_6), .pin7(M6),
    .pin8(1'b0), .pin9(M7), .pin10(STEP_7), .pin11(REL_7), .pin12(RB[7]), .pin13(1'b0), .pin14(MODE_0),
    .pin15(RESET), .pin16(1'b1));
  _74153 _74153_2 (
    .pin1(RESET), .pin2(MODE_1), .pin3(1'b0), .pin4(RB[4]), .pin5(REL_4), .pin6(STEP_4), .pin7(M4),
    .pin8(1'b0), .pin9(M5), .pin10(STEP_5), .pin11(REL_5), .pin12(RB[5]), .pin13(1'b0), .pin14(MODE_0),
    .pin15(RESET), .pin16(1'b1));
  _74153 _74153_3 (
    .pin1(RESET), .pin2(MODE_1), .pin3(1'b0), .pin4(RB[2]), .pin5(REL_2), .pin6(STEP_2), .pin7(M2),
    .pin8(1'b0), .pin9(M3), .pin10(STEP_3), .pin11(REL_3), .pin12(RB[3]), .pin13(1'b0), .pin14(MODE_0),
    .pin15(RESET), .pin16(1'b1));
  _74153 _74153_4 (
    .pin1(RESET), .pin2(MODE_1), .pin3(1'b0), .pin4(RB[0]), .pin5(REL_0), .pin6(STEP_0_t), .pin7(M0),
    .pin8(1'b0), .pin9(M1), .pin10(STEP_1_t), .pin11(REL_1), .pin12(RB[1]), .pin13(1'b0), .pin14(MODE_0),
    .pin15(RESET), .pin16(1'b1));
  _7483Real _7483real_1 (
    .pin1(A0[7]), .pin2(REL_6), .pin3(A0[6]), .pin4(RB[6]), .pin5(1'b1), .pin6(REL_5), .pin7(RB[5]),
    .pin8(A0[5]), .pin9(REL_4), .pin10(A0[4]), .pin11(RB[4]), .pin12(1'b0), .pin13(_7483real_1_pin13),
    .pin14(REL_CARRY), .pin15(REL_7), .pin16(RB[7]));
  _7483Real _7483real_2 (
    .pin1(A0[7]), .pin2(STEP_6), .pin3(A0[6]), .pin4(1'b0), .pin5(1'b1), .pin6(STEP_5), .pin7(1'b0),
    .pin8(A0[5]), .pin9(STEP_4), .pin10(A0[4]), .pin11(1'b0), .pin12(1'b0), .pin13(_7483real_2_pin13),
    .pin14(STEP_CARRY), .pin15(STEP_7), .pin16(1'b0));
  _74377 _74377_1 (
    .pin1(nR_ENABLE), .pin2(A0[7]), .pin3(M7), .pin4(M5), .pin5(A0[5]), .pin6(A0[3]), .pin7(M3), .pin8(M1),
    .pin9(A0[1]), .pin10(1'b0), .pin11(CLK), .pin12(A0[0]), .pin13(M0), .pin14(M2), .pin15(A0[2]),
    .pin16(A0[4]), .pin17(M4), .pin18(M6), .pin19(A0[6]), .pin20(1'b1));
  _7483Real _7483real_3 (
    .pin1(A0[3]), .pin2(REL_2), .pin3(A0[2]), .pin4(RB[2]), .pin5(1'b1), .pin6(REL_1), .pin7(RB[1]),
    .pin8(A0[1]), .pin9(REL_0), .pin10(A0[0]), .pin11(RB[0]), .pin12(1'b0), .pin13(1'b0),
    .pin14(_7483real_1_pin13), .pin15(REL_3), .pin16(RB[3]));
  _7483Real _7483real_4 (
    .pin1(A0[3]), .pin2(STEP_2), .pin3(A0[2]), .pin4(1'b0), .pin5(1'b1), .pin6(STEP_1_t), .pin7(STEP_1),
    .pin8(A0[1]), .pin9(STEP_0_t), .pin10(A0[0]), .pin11(STEP_0), .pin12(1'b0), .pin13(1'b1),
    .pin14(_7483real_2_pin13), .pin15(STEP_3), .pin16(1'b0));

  // Other names for the same wires on the sheet: A_0 = A0[0]; A_1 = A0[1]; A_2 = A0[2]; A_3 = A0[3]; A_4 = A0[4];
  //   A_5 = A0[5]; A_6 = A0[6]; A_7 = A0[7]; ABS_0 = RB[0]; RB_0 = RB[0]; ABS_1 = RB[1]; RB_1 = RB[1]; ABS_2 = RB[2];
  //   RB_2 = RB[2]; ABS_3 = RB[3]; RB_3 = RB[3]; ABS_4 = RB[4]; RB_4 = RB[4]; ABS_5 = RB[5]; RB_5 = RB[5];
  //   ABS_6 = RB[6]; RB_6 = RB[6]; ABS_7 = RB[7]; RB_7 = RB[7]; STEP0 = STEP_0; STEP1 = STEP_1

  // Notes on the sheet:
  //   RESET: default 1
  //   STEP_0: default 1
endmodule
