// Digital circuit program memory 2.dig as structural Verilog
module program_memory_2 (
  input  nCLK,
  input  CLK,
  input  nRESET,
  input  RESET,
  input  [15:0] PC,
  output [15:0] PM
);

  PowerSupply powersupply_1 (.VDD(1'b1), .GND(1'b0));
  _74273 _74273_1 (
    .pin1(nRESET), .pin2(PM[8]), .pin3(PM[0]), .pin4(PM[1]), .pin5(PM[9]), .pin6(PM[10]), .pin7(PM[2]),
    .pin8(PM[3]), .pin9(PM[11]), .pin10(1'b0), .pin11(nCLK), .pin12(PM[12]), .pin13(PM[4]), .pin14(PM[5]),
    .pin15(PM[13]), .pin16(PM[14]), .pin17(PM[6]), .pin18(PM[7]), .pin19(PM[15]), .pin20(1'b1));
  eeprom eeprom_1 (
    .nCE(1'b0), .nOE(RESET), .nWE(1'b1), .VCC(1'b1), .GND(1'b0), .I_O0(PM[0]), .I_O1(PM[1]), .I_O2(PM[2]),
    .I_O3(PM[3]), .I_O4(PM[4]), .I_O5(PM[5]), .I_O6(PM[6]), .I_O7(PM[7]), .A0(CLK), .A1(PC[1]), .A2(PC[2]),
    .A3(PC[3]), .A4(PC[4]), .A5(PC[5]), .A6(PC[6]), .A7(PC[7]), .A8(PC[8]), .A9(PC[9]), .A10(PC[10]),
    .A11(PC[11]), .A12(PC[12]), .A13(PC[13]), .A14(PC[14]), .A15(PC[15]));

  // Other names for the same wires on the sheet: Q0 = PC[0]; Q1 = PC[1]; Q2 = PC[2]; Q3 = PC[3]; Q4 = PC[4];
  //   Q5 = PC[5]; Q6 = PC[6]; Q7 = PC[7]; Q8 = PC[8]; Q9 = PC[9]; Q10 = PC[10]; Q11 = PC[11]; Q12 = PC[12];
  //   Q13 = PC[13]; Q14 = PC[14]; Q15 = PC[15]
endmodule
