// Digital circuit clock pc pm rf v24.dig as structural Verilog
module clock_pc_pm_rf_v24 (
  input  STEP0,
  input  STEP1,
  input  nCLK_ENABLE,
  input  AUTO,
  input  VCC,
  input  GND,
  input  [7:0] WA_IN,
  output S_CARRY,
  output A0,
  output A1,
  output A2,
  output A3,
  output A4,
  output A5,
  output A6,
  output A7,
  output R_CARRY,
  output PM8,
  output PM9,
  output PM10,
  output PM11,
  output PM12,
  output PM13,
  output PM14,
  output PM15,
  output PM0,
  output PM1,
  output PM2,
  output PM3,
  output PM4,
  output PM5,
  output PM6,
  output PM7,
  output nRESET,
  output CLK,
  output out_33,
  output out_34,
  output RESET,
  output out_38,
  output RA_0,
  output RA_1,
  output RA_2,
  output RA_3,
  output RA_4,
  output RA_5,
  output RA_6,
  output RA_7,
  output RB_0,
  output RB_1,
  output RB_2,
  output RB_3,
  output RB_4,
  output RB_5,
  output RB_6,
  output RB_7,
  output RC_0,
  output RC_1,
  output RC_2,
  output RC_3,
  output RC_4,
  output RC_5,
  output RC_6,
  output RC_7,
  output R1_0,
  output R1_1,
  output R1_2,
  output R1_3,
  output R1_4,
  output R1_5,
  output R1_6,
  output R1_7,
  output R2_0,
  output R2_1,
  output R2_2,
  output R2_3,
  output R2_4,
  output R2_5,
  output R2_6,
  output R2_7,
  output R3_0,
  output R3_1,
  output R3_2,
  output R3_3,
  output R3_4,
  output R3_5,
  output R3_6,
  output R3_7,
  output R4_0,
  output R4_1,
  output R4_2,
  output R4_3,
  output R4_4,
  output R4_5,
  output R4_6,
  output R4_7,
  output R5_0,
  output R5_1,
  output R5_2,
  output R5_3,
  output R5_4,
  output R5_5,
  output R5_6,
  output R5_7,
  output R6_0,
  output R6_1,
  output R6_2,
  output R6_3,
  output R6_4,
  output R6_5,
  output R6_6,
  output R6_7,
  output R7_0,
  output R7_1,
  output R7_2,
  output R7_3,
  output R7_4,
  output R7_5,
  output R7_6,
  output R7_7
);

  wire _7400_1_pin3, _7400_1_pin6, _7400_3_pin3, _7400_3_pin6, _7414_1_pin8, _7483real_1_pin2,
       _7483real_1_pin6, _7483real_1_pin9, _7483real_1_pin13, _7483real_1_pin15, _7483real_2_pin2,
       _7483real_2_pin6, _7483real_2_pin9, _7483real_2_pin15, _7483real_3_pin13, _7483real_4_pin6,
       _7483real_4_pin9, _74153_1_pin1, _74153_1_pin6, _74153_1_pin10, _74153_2_pin6, _74153_2_pin10,
       _74153_3_pin6, _74153_3_pin10, _74173_1_pin3, _74173_1_pin4, _74173_1_pin5, BTN_BREAK, BTN_RESET,
       BTN_RUN, M0, M1, M2, M3, M4, M5, M6, M7, nCLK;
  wire [7:0] IMM;

  PowerSupply powersupply_1 (.VDD(VCC), .GND(GND));
  Button SINGLE (.out(out_38));
  Button #(.activeLow("true")) BREAK (.out(BTN_BREAK));
  Button #(.activeLow("true")) RUN (.out(BTN_RUN));
  Button u_RESET (.out(BTN_RESET));
  register_file register_file_1 (
    .WA(WA_IN), .WA_ADDR({PM7, PM6, PM5, PM4}), .RB_ADDR({PM11, PM10, PM9, PM8}), .CLK(CLK), .IS_IMM(PM3),
    .IMM(IMM), .RA({RA_7, RA_6, RA_5, RA_4, RA_3, RA_2, RA_1, RA_0}),
    .RB({RB_7, RB_6, RB_5, RB_4, RB_3, RB_2, RB_1, RB_0}),
    .RC({RC_7, RC_6, RC_5, RC_4, RC_3, RC_2, RC_1, RC_0}),
    .R_1({R1_7, R1_6, R1_5, R1_4, R1_3, R1_2, R1_1, R1_0}),
    .R_2({R2_7, R2_6, R2_5, R2_4, R2_3, R2_2, R2_1, R2_0}),
    .R_3({R3_7, R3_6, R3_5, R3_4, R3_3, R3_2, R3_1, R3_0}),
    .R_4({R4_7, R4_6, R4_5, R4_4, R4_3, R4_2, R4_1, R4_0}),
    .R_5({R5_7, R5_6, R5_5, R5_4, R5_3, R5_2, R5_1, R5_0}),
    .R_6({R6_7, R6_6, R6_5, R6_4, R6_3, R6_2, R6_1, R6_0}),
    .R_7({R7_7, R7_6, R7_5, R7_4, R7_3, R7_2, R7_1, R7_0}));
  _7483Real _7483real_1 (
    .pin1(A7), .pin2(_7483real_1_pin2), .pin3(A6), .pin4(RB_6), .pin5(VCC), .pin6(_7483real_1_pin6),
    .pin7(RB_5), .pin8(A5), .pin9(_7483real_1_pin9), .pin10(A4), .pin11(RB_4), .pin12(GND),
    .pin13(_7483real_1_pin13), .pin14(R_CARRY), .pin15(_7483real_1_pin15), .pin16(RB_7));
  _7400 _7400_1 (
    .pin1(out_38), .pin2(out_33), .pin3(_7400_1_pin3), .pin4(AUTO), .pin5(out_34), .pin6(_7400_1_pin6),
    .pin7(GND), .pin8(out_34), .pin9(BTN_RUN), .pin10(out_33), .pin11(out_33), .pin12(out_34),
    .pin13(BTN_BREAK), .pin14(VCC));
  _74153 _74153_1 (
    .pin1(_74153_1_pin1), .pin2(PM1), .pin3(GND), .pin4(RB_6), .pin5(_7483real_1_pin2), .pin6(_74153_1_pin6),
    .pin7(M6), .pin8(GND), .pin9(M7), .pin10(_74153_1_pin10), .pin11(_7483real_1_pin15), .pin12(RB_7),
    .pin13(GND), .pin14(PM0), .pin15(_74153_1_pin1), .pin16(VCC));
  _7483Real _7483real_2 (
    .pin1(A3), .pin2(_7483real_2_pin2), .pin3(A2), .pin4(RB_2), .pin5(VCC), .pin6(_7483real_2_pin6),
    .pin7(RB_1), .pin8(A1), .pin9(_7483real_2_pin9), .pin10(A0), .pin11(RB_0), .pin12(GND), .pin13(GND),
    .pin14(_7483real_1_pin13), .pin15(_7483real_2_pin15), .pin16(RB_3));
  _7400 _7400_2 (
    .pin1(_7400_1_pin3), .pin2(_7400_1_pin6), .pin3(CLK), .pin4(nRESET), .pin5(nRESET), .pin6(RESET),
    .pin7(GND), .pin9(VCC), .pin10(VCC), .pin12(VCC), .pin13(VCC), .pin14(VCC));  // open: pin8, pin11
  _74153 _74153_2 (
    .pin1(_74153_1_pin1), .pin2(PM1), .pin3(GND), .pin4(RB_4), .pin5(_7483real_1_pin9), .pin6(_74153_2_pin6),
    .pin7(M4), .pin8(GND), .pin9(M5), .pin10(_74153_2_pin10), .pin11(_7483real_1_pin6), .pin12(RB_5),
    .pin13(GND), .pin14(PM0), .pin15(_74153_1_pin1), .pin16(VCC));
  _74173 _74173_1 (
    .pin1(GND), .pin2(GND), .pin3(_74173_1_pin3), .pin4(_74173_1_pin4), .pin5(_74173_1_pin5), .pin6(nRESET),
    .pin7(CLK), .pin8(GND), .pin9(GND), .pin10(GND), .pin11(_74173_1_pin5), .pin12(_74173_1_pin4),
    .pin13(_74173_1_pin3), .pin14(VCC), .pin15(BTN_RESET), .pin16(VCC));
  _7483Real _7483real_3 (
    .pin1(A7), .pin2(_74153_1_pin6), .pin3(A6), .pin4(GND), .pin5(VCC), .pin6(_74153_2_pin10), .pin7(GND),
    .pin8(A5), .pin9(_74153_2_pin6), .pin10(A4), .pin11(GND), .pin12(GND), .pin13(_7483real_3_pin13),
    .pin14(S_CARRY), .pin15(_74153_1_pin10), .pin16(GND));
  _74273 _74273_1 (
    .pin1(nRESET), .pin2(PM8), .pin3(PM0), .pin4(PM1), .pin5(PM9), .pin6(PM10), .pin7(PM2), .pin8(PM3),
    .pin9(PM11), .pin10(GND), .pin11(nCLK), .pin12(PM12), .pin13(PM4), .pin14(PM5), .pin15(PM13),
    .pin16(PM14), .pin17(PM6), .pin18(PM7), .pin19(PM15), .pin20(VCC));
  _7414 _7414_1 (
    .pin1(GND), .pin3(GND), .pin5(GND), .pin7(GND), .pin8(_7414_1_pin8), .pin9(PM3), .pin11(GND),
    .pin13(GND), .pin14(VCC));  // open: pin2, pin4, pin6, pin10, pin12
  _74153 _74153_3 (
    .pin1(_74153_1_pin1), .pin2(PM1), .pin3(GND), .pin4(RB_2), .pin5(_7483real_2_pin2), .pin6(_74153_3_pin6),
    .pin7(M2), .pin8(GND), .pin9(M3), .pin10(_74153_3_pin10), .pin11(_7483real_2_pin15), .pin12(RB_3),
    .pin13(GND), .pin14(PM0), .pin15(_74153_1_pin1), .pin16(VCC));
  PullDown pulldown_1 (.out(_74173_1_pin3));
  PullDown pulldown_2 (.out(_74173_1_pin4));
  PullDown pulldown_3 (.out(_74173_1_pin5));
  _74245 _74245_1 (
    .pin1(VCC), .pin2(PM15), .pin3(PM14), .pin4(PM13), .pin5(PM12), .pin6(PM11), .pin7(PM10), .pin8(PM9),
    .pin9(PM8), .pin10(GND), .pin11(IMM[0]), .pin12(IMM[1]), .pin13(IMM[2]), .pin14(IMM[3]), .pin15(IMM[4]),
    .pin16(IMM[5]), .pin17(IMM[6]), .pin18(IMM[7]), .pin19(_7414_1_pin8), .pin20(VCC));
  _7483Real _7483real_4 (
    .pin1(A3), .pin2(_74153_3_pin6), .pin3(A2), .pin4(GND), .pin5(VCC), .pin6(_7483real_4_pin6),
    .pin7(STEP1), .pin8(A1), .pin9(_7483real_4_pin9), .pin10(A0), .pin11(STEP0), .pin12(GND), .pin13(GND),
    .pin14(_7483real_3_pin13), .pin15(_74153_3_pin10), .pin16(GND));
  _74153 _74153_4 (
    .pin1(_74153_1_pin1), .pin2(PM1), .pin3(GND), .pin4(RB_0), .pin5(_7483real_2_pin9),
    .pin6(_7483real_4_pin9), .pin7(M0), .pin8(GND), .pin9(M1), .pin10(_7483real_4_pin6),
    .pin11(_7483real_2_pin6), .pin12(RB_1), .pin13(GND), .pin14(PM0), .pin15(_74153_1_pin1), .pin16(VCC));
  eeprom eeprom_1 (
    .nCE(GND), .nOE(RESET), .nWE(VCC), .VCC(VCC), .GND(GND), .I_O0(PM0), .I_O1(PM1), .I_O2(PM2), .I_O3(PM3),
    .I_O4(PM4), .I_O5(PM5), .I_O6(PM6), .I_O7(PM7), .A0(CLK), .A1(A1), .A2(A2), .A3(A3), .A4(A4), .A5(A5),
    .A6(A6), .A7(A7), .A8(GND), .A9(GND), .A10(GND), .A11(GND), .A12(GND), .A13(GND), .A14(GND), .A15(GND));
  _7400 _7400_3 (
    .pin1(nRESET), .pin2(nCLK_ENABLE), .pin3(_7400_3_pin3), .pin4(_7400_3_pin3), .pin5(_7400_3_pin3),
    .pin6(_7400_3_pin6), .pin7(GND), .pin8(nCLK), .pin9(CLK), .pin10(CLK), .pin11(_74153_1_pin1),
    .pin12(nRESET), .pin13(nRESET), .pin14(VCC));
  _74377 _74377_1 (
    .pin1(_7400_3_pin6), .pin2(A7), .pin3(M7), .pin4(M5), .pin5(A5), .pin6(A3), .pin7(M3), .pin8(M1),
    .pin9(A1), .pin10(GND), .pin11(CLK), .pin12(A0), .pin13(M0), .pin14(M2), .pin15(A2), .pin16(A4),
    .pin17(M4), .pin18(M6), .pin19(A6), .pin20(VCC));

  // Other names for the same wires on the sheet: BTN_SINGLE = out_38; CLK_AUTO = AUTO; IS_IMM = PM3;
  //   LED_BREAK = out_33; LED_RUN = out_34; Q0 = A0; Q1 = A1; Q2 = A2; Q3 = A3; Q4 = A4; Q5 = A5; Q6 = A6; Q7 = A7;
  //   R_1[7:0] = {R1_7, R1_6, R1_5, R1_4, R1_3, R1_2, R1_1, R1_0};
  //   R_2[7:0] = {R2_7, R2_6, R2_5, R2_4, R2_3, R2_2, R2_1, R2_0};
  //   R_3[7:0] = {R3_7, R3_6, R3_5, R3_4, R3_3, R3_2, R3_1, R3_0};
  //   R_4[7:0] = {R4_7, R4_6, R4_5, R4_4, R4_3, R4_2, R4_1, R4_0};
  //   R_5[7:0] = {R5_7, R5_6, R5_5, R5_4, R5_3, R5_2, R5_1, R5_0};
  //   R_6[7:0] = {R6_7, R6_6, R6_5, R6_4, R6_3, R6_2, R6_1, R6_0};
  //   R_7[7:0] = {R7_7, R7_6, R7_5, R7_4, R7_3, R7_2, R7_1, R7_0};
  //   RA[7:0] = {RA_7, RA_6, RA_5, RA_4, RA_3, RA_2, RA_1, RA_0};
  //   RB[7:0] = {RB_7, RB_6, RB_5, RB_4, RB_3, RB_2, RB_1, RB_0};
  //   RC[7:0] = {RC_7, RC_6, RC_5, RC_4, RC_3, RC_2, RC_1, RC_0}

  // Notes on the sheet:
  //   STEP0: default 1
  //   AUTO: Hz: 20
  //   VCC: default 1
  //   Relative jumps add RD to D.
  //   For backwards jumps, use
  //   2's compliment arithmetic.
  //   The step counter by default adds 1 to D.
  //   We can increase to a maximum of 4
  //   by setting STEP0 and STEP1.
endmodule
