// Digital circuit register.dig as structural Verilog
module register (
  input  CLK,
  input  [7:0] WA,
  input  nRA_ENABLE,
  input  nRB_ENABLE,
  input  nRC_ENABLE,
  input  nWA_ENABLE,
  output [7:0] REG,
  output [7:0] RA,
  output [7:0] RB,
  output [7:0] RC
);

  wire _74245_1_pin11, _74245_1_pin12, _74245_1_pin13, _74245_1_pin14, _74245_1_pin15, _74245_1_pin16,
       _74245_1_pin17, _74245_1_pin18;

  PowerSupply powersupply_1 (.VDD(1'b1), .GND(1'b0));
  _74245 _74245_1 (
    .pin1(1'b1), .pin2(WA[7]), .pin3(WA[6]), .pin4(WA[5]), .pin5(WA[4]), .pin6(WA[3]), .pin7(WA[2]),
    .pin8(WA[1]), .pin9(WA[0]), .pin10(1'b0), .pin11(_74245_1_pin11), .pin12(_74245_1_pin12),
    .pin13(_74245_1_pin13), .pin14(_74245_1_pin14), .pin15(_74245_1_pin15), .pin16(_74245_1_pin16),
    .pin17(_74245_1_pin17), .pin18(_74245_1_pin18), .pin19(nWA_ENABLE), .pin20(1'b1));
  _74377 _74377_1 (
    .pin1(nWA_ENABLE), .pin2(REG[6]), .pin3(_74245_1_pin17), .pin4(_74245_1_pin15), .pin5(REG[4]),
    .pin6(REG[2]), .pin7(_74245_1_pin13), .pin8(_74245_1_pin11), .pin9(REG[0]), .pin10(1'b0), .pin11(CLK),
    .pin12(REG[1]), .pin13(_74245_1_pin12), .pin14(_74245_1_pin14), .pin15(REG[3]), .pin16(REG[5]),
    .pin17(_74245_1_pin16), .pin18(_74245_1_pin18), .pin19(REG[7]), .pin20(1'b1));
  _74245 _74245_2 (
    .pin1(1'b0), .pin2(RA[7]), .pin3(RA[6]), .pin4(RA[5]), .pin5(RA[4]), .pin6(RA[3]), .pin7(RA[2]),
    .pin8(RA[1]), .pin9(RA[0]), .pin10(1'b0), .pin11(REG[0]), .pin12(REG[1]), .pin13(REG[2]), .pin14(REG[3]),
    .pin15(REG[4]), .pin16(REG[5]), .pin17(REG[6]), .pin18(REG[7]), .pin19(nRA_ENABLE), .pin20(1'b1));
  _74245 _74245_3 (
    .pin1(1'b0), .pin2(RB[7]), .pin3(RB[6]), .pin4(RB[5]), .pin5(RB[4]), .pin6(RB[3]), .pin7(RB[2]),
    .pin8(RB[1]), .pin9(RB[0]), .pin10(1'b0), .pin11(REG[0]), .pin12(REG[1]), .pin13(REG[2]), .pin14(REG[3]),
    .pin15(REG[4]), .pin16(REG[5]), .pin17(REG[6]), .pin18(REG[7]), .pin19(nRB_ENABLE), .pin20(1'b1));
  _74245 _74245_4 (
    .pin1(1'b0), .pin2(RC[7]), .pin3(RC[6]), .pin4(RC[5]), .pin5(RC[4]), .pin6(RC[3]), .pin7(RC[2]),
    .pin8(RC[1]), .pin9(RC[0]), .pin10(1'b0), .pin11(REG[0]), .pin12(REG[1]), .pin13(REG[2]), .pin14(REG[3]),
    .pin15(REG[4]), .pin16(REG[5]), .pin17(REG[6]), .pin18(REG[7]), .pin19(nRC_ENABLE), .pin20(1'b1));
endmodule
