// Digital circuit alu.dig as structural Verilog
module alu (
  input  [7:0] RHS,
  input  [7:0] LHS,
  input  USECARRY,
  input  USESUB,
  input  WRITEBACK_ALU,
  input  CLK,
  output F_CARRYOUT,
  output [7:0] SUM
);

  wire _74283_1_pin7, ALU_CARRYIN, CARRY_OUT, RHS_D0, RHS_D1, RHS_D2, RHS_D3, RHS_D4, RHS_D5, RHS_D6, RHS_D7;

  _74377 _74377_1 (
    .pin1(WRITEBACK_ALU), .pin2(CARRY_OUT), .pin3(F_CARRYOUT), .pin4(1'b1), .pin7(1'b1), .pin8(1'b1),
    .pin10(1'b0), .pin11(CLK), .pin13(1'b1), .pin14(1'b1), .pin17(1'b1), .pin18(1'b1), .pin20(1'b1));  // open: pin5, pin6, pin9, pin12, pin15, pin16, pin19
  PowerSupply powersupply_1 (.VDD(1'b1), .GND(1'b0));
  _74153 _74153_1 (
    .pin1(1'b0), .pin2(USESUB), .pin3(CARRY_OUT), .pin4(1'b1), .pin5(CARRY_OUT), .pin6(1'b0),
    .pin7(ALU_CARRYIN), .pin8(1'b0), .pin10(1'b1), .pin11(1'b1), .pin12(1'b1), .pin13(1'b1),
    .pin14(USECARRY), .pin15(1'b0), .pin16(1'b1));  // open: pin9
  _74283 _74283_1 (
    .pin1(SUM[5]), .pin2(RHS_D5), .pin3(LHS[5]), .pin4(SUM[4]), .pin5(LHS[4]), .pin6(RHS_D4),
    .pin7(_74283_1_pin7), .pin8(1'b0), .pin9(F_CARRYOUT), .pin10(SUM[7]), .pin11(RHS_D7), .pin12(LHS[7]),
    .pin13(SUM[6]), .pin14(LHS[6]), .pin15(RHS_D6), .pin16(1'b1));
  _74283 _74283_2 (
    .pin1(SUM[1]), .pin2(RHS_D1), .pin3(LHS[1]), .pin4(SUM[0]), .pin5(LHS[0]), .pin6(RHS_D0),
    .pin7(ALU_CARRYIN), .pin8(1'b0), .pin9(_74283_1_pin7), .pin10(SUM[3]), .pin11(RHS_D3), .pin12(LHS[3]),
    .pin13(SUM[2]), .pin14(LHS[2]), .pin15(RHS_D2), .pin16(1'b1));
  _7486 _7486_1 (
    .pin1(USESUB), .pin2(RHS[4]), .pin3(RHS_D4), .pin4(USESUB), .pin5(RHS[5]), .pin6(RHS_D5), .pin7(1'b0),
    .pin8(RHS_D6), .pin9(USESUB), .pin10(RHS[6]), .pin11(RHS_D7), .pin12(USESUB), .pin13(RHS[7]), .pin14(1'b1));
  _7486 _7486_2 (
    .pin1(USESUB), .pin2(RHS[0]), .pin3(RHS_D0), .pin4(USESUB), .pin5(RHS[1]), .pin6(RHS_D1), .pin7(1'b0),
    .pin8(RHS_D2), .pin9(USESUB), .pin10(RHS[2]), .pin11(RHS_D3), .pin12(USESUB), .pin13(RHS[3]), .pin14(1'b1));

  // Other names for the same wires on the sheet: C_IN = USECARRY; C_OUT = F_CARRYOUT; F_ENABLE = WRITEBACK_ALU;
  //   LHS_0 = LHS[0]; LHS_1 = LHS[1]; LHS_2 = LHS[2]; LHS_3 = LHS[3]; LHS_4 = LHS[4]; LHS_5 = LHS[5]; LHS_6 = LHS[6];
  //   LHS_7 = LHS[7]; RHS_0 = RHS[0]; RHS_1 = RHS[1]; RHS_2 = RHS[2]; RHS_3 = RHS[3]; RHS_4 = RHS[4]; RHS_5 = RHS[5];
  //   RHS_6 = RHS[6]; RHS_7 = RHS[7]; SUB = USESUB; SUM_0 = SUM[0]; SUM_1 = SUM[1]; SUM_2 = SUM[2]; SUM_3 = SUM[3];
  //   SUM_4 = SUM[4]; SUM_5 = SUM[5]; SUM_6 = SUM[6]; SUM_7 = SUM[7]
endmodule
