// Digital circuit build 2.dig as structural Verilog
module build_2 (
  input  STEP0,
  input  STEP1,
  input  AUTO,
  input  VCC,
  input  GND,
  input  [7:0] WA_IN,
  output A0,
  output A1,
  output A2,
  output A3,
  output A4,
  output A5,
  output A6,
  output A7,
  output PM8,
  output PM9,
  output PM10,
  output PM11,
  output PM12,
  output PM13,
  output PM14,
  output PM15,
  output PM0,
  output PM1,
  output PM2,
  output PM3,
  output PM4,
  output PM5,
  output PM6,
  output PM7,
  output nRESET,
  output CLK,
  output out_30,
  output out_31,
  output RESET,
  output out_35,
  output RA_0,
  output RA_1,
  output RA_2,
  output RA_3,
  output RA_4,
  output RA_5,
  output RA_6,
  output RA_7,
  output RB_0,
  output RB_1,
  output RB_2,
  output RB_3,
  output RB_4,
  output RB_5,
  output RB_6,
  output RB_7,
  output RC_0,
  output RC_1,
  output RC_2,
  output RC_3,
  output RC_4,
  output RC_5,
  output RC_6,
  output RC_7,
  output R1_0,
  output R1_1,
  output R1_2,
  output R1_3,
  output R1_4,
  output R1_5,
  output R1_6,
  output R1_7,
  output R2_0,
  output R2_1,
  output R2_2,
  output R2_3,
  output R2_4,
  output R2_5,
  output R2_6,
  output R2_7,
  output R3_0,
  output R3_1,
  output R3_2,
  output R3_3,
  output R3_4,
  output R3_5,
  output R3_6,
  output R3_7,
  output R4_0,
  output R4_1,
  output R4_2,
  output R4_3,
  output R4_4,
  output R4_5,
  output R4_6,
  output R4_7,
  output R5_0,
  output R5_1,
  output R5_2,
  output R5_3,
  output R5_4,
  output R5_5,
  output R5_6,
  output R5_7,
  output R6_0,
  output R6_1,
  output R6_2,
  output R6_3,
  output R6_4,
  output R6_5,
  output R6_6,
  output R6_7,
  output R7_0,
  output R7_1,
  output R7_2,
  output R7_3,
  output R7_4,
  output R7_5,
  output R7_6,
  output R7_7,
  output A8,
  output A9,
  output A10,
  output A11,
  output A12,
  output A13,
  output A14,
  output A15
);

  wire BTN_BREAK, BTN_RESET, BTN_RUN, nCLK;
  wire [7:0] IMM_OUT;

  alu alu_1 ();  // open: RHS, LHS, USECARRY, USESUB, WRITEBACK_ALU, CLK, F_CARRYOUT, SUM
  PowerSupply powersupply_1 (.VDD(VCC), .GND(GND));
  Button SINGLE (.out(out_35));
  register_file_2 register_file_2_1 (
    .WA_ADDR({PM7, PM6, PM5, PM4}), .RB_ADDR({PM11, PM10, PM9, PM8}), .CLK(CLK), .IS_IMM(PM3), .IMM(IMM_OUT),
    .WA(WA_IN), .RA({RA_7, RA_6, RA_5, RA_4, RA_3, RA_2, RA_1, RA_0}),
    .RB({RB_7, RB_6, RB_5, RB_4, RB_3, RB_2, RB_1, RB_0}),
    .RC({RC_7, RC_6, RC_5, RC_4, RC_3, RC_2, RC_1, RC_0}),
    .R_1({R1_7, R1_6, R1_5, R1_4, R1_3, R1_2, R1_1, R1_0}),
    .R_2({R2_7, R2_6, R2_5, R2_4, R2_3, R2_2, R2_1, R2_0}),
    .R_3({R3_7, R3_6, R3_5, R3_4, R3_3, R3_2, R3_1, R3_0}),
    .R_4({R4_7, R4_6, R4_5, R4_4, R4_3, R4_2, R4_1, R4_0}),
    .R_5({R5_7, R5_6, R5_5, R5_4, R5_3, R5_2, R5_1, R5_0}),
    .R_6({R6_7, R6_6, R6_5, R6_4, R6_3, R6_2, R6_1, R6_0}),
    .R_7({R7_7, R7_6, R7_5, R7_4, R7_3, R7_2, R7_1, R7_0}));
  program_memory_2 program_memory_2_1 (
    .nCLK(nCLK), .CLK(CLK), .nRESET(nRESET), .RESET(RESET),
    .PC({A15, A14, A13, A12, A11, A10, A9, A8, A7, A6, A5, A4, A3, A2, A1, A0}),
    .PM({PM15, PM14, PM13, PM12, PM11, PM10, PM9, PM8, PM7, PM6, PM5, PM4, PM3, PM2, PM1, PM0}));
  immediate immediate_1 (.IMM_IN({PM15, PM14, PM13, PM12, PM11, PM10, PM9, PM8}), .IS_IMM(PM3), .IMM_OUT(IMM_OUT));
  Button #(.activeLow("true")) BREAK (.out(BTN_BREAK));
  Button #(.activeLow("true")) RUN (.out(BTN_RUN));
  Button u_RESET (.out(BTN_RESET));
  program_counter_2___DEBUG program_counter_2___debug_1 (
    .STEPSIZE_1(STEP1), .STEPSIZE_0(STEP0), .SEL_1(PM1), .SEL_0(PM0), .nENABLE(GND), .nRESET(nRESET),
    .CLK(CLK),
    .ABSADDR({RC_7, RC_6, RC_5, RC_4, RC_3, RC_2, RC_1, RC_0, RB_7, RB_6, RB_5, RB_4, RB_3, RB_2, RB_1, RB_0}),
    .RELBASE({A15, A14, A13, A12, A11, A10, A9, A8, A7, A6, A5, A4, A3, A2, A1, A0}),
    .RELOFFSET({RB_7, RB_6, RB_5, RB_4, RB_3, RB_2, RB_1, RB_0}),
    .PC({A15, A14, A13, A12, A11, A10, A9, A8, A7, A6, A5, A4, A3, A2, A1, A0}), .nCLK(nCLK));  // open: STEPADDR
  clock clock_1 (
    .CLK_AUTO(AUTO), .BTN_SINGLE(out_35), .BTN_BREAK(BTN_BREAK), .BTN_RUN(BTN_RUN), .BTN_RESET(BTN_RESET),
    .LED_BREAK(out_30), .LED_RUN(out_31), .RESET(RESET), .nRESET(nRESET), .CLK(CLK));

  // Other names for the same wires on the sheet: BTN_SINGLE = out_35; CLK_AUTO = AUTO; LED_BREAK = out_30;
  //   LED_RUN = out_31; nCLK_ENABLE = GND;
  //   PC[15:0] = {A15, A14, A13, A12, A11, A10, A9, A8, A7, A6, A5, A4, A3, A2, A1, A0}; MODE0 = PM0; MODE1 = PM1;
  //   IS_IMM = PM3; DEST_ADDR[3:0] = {PM7, PM6, PM5, PM4}; IMM[7:0] = {PM15, PM14, PM13, PM12, PM11, PM10, PM9, PM8};
  //   SRC_ADDR[3:0] = {PM11, PM10, PM9, PM8}; R_1[7:0] = {R1_7, R1_6, R1_5, R1_4, R1_3, R1_2, R1_1, R1_0};
  //   R_2[7:0] = {R2_7, R2_6, R2_5, R2_4, R2_3, R2_2, R2_1, R2_0};
  //   R_3[7:0] = {R3_7, R3_6, R3_5, R3_4, R3_3, R3_2, R3_1, R3_0};
  //   R_4[7:0] = {R4_7, R4_6, R4_5, R4_4, R4_3, R4_2, R4_1, R4_0};
  //   R_5[7:0] = {R5_7, R5_6, R5_5, R5_4, R5_3, R5_2, R5_1, R5_0};
  //   R_6[7:0] = {R6_7, R6_6, R6_5, R6_4, R6_3, R6_2, R6_1, R6_0};
  //   R_7[7:0] = {R7_7, R7_6, R7_5, R7_4, R7_3, R7_2, R7_1, R7_0};
  //   RA[7:0] = {RA_7, RA_6, RA_5, RA_4, RA_3, RA_2, RA_1, RA_0};
  //   ABSADDR[15:0] = {RC_7, RC_6, RC_5, RC_4, RC_3, RC_2, RC_1, RC_0, RB_7, RB_6, RB_5, RB_4, RB_3, RB_2, RB_1, RB_0};
  //   RB[7:0] = {RB_7, RB_6, RB_5, RB_4, RB_3, RB_2, RB_1, RB_0};
  //   RC[7:0] = {RC_7, RC_6, RC_5, RC_4, RC_3, RC_2, RC_1, RC_0}

  // Notes on the sheet:
  //   STEP0: default 1
  //   AUTO: Hz: 20
  //   VCC: default 1
  //   Relative jumps add RD to D.
  //   For backwards jumps, use
  //   2's compliment arithmetic.
  //   The step counter by default adds 1 to D.
  //   We can increase to a maximum of 4
  //   by setting STEP0 and STEP1.
  //   Next step is probably ALU.
  //   Maybe uses PM2 to toggle ALU mode.
  //   (or all other instructions).
  //   Not sure about this.
  //   JF: I've been wondering about that third read_data bus. My initial idea was to connect it to the write_data bus with some logic to create a read/write bus (with some logic to allow the it to copy) but using it as the h_byte  for 16b addressing is cool. Shouldn't be too hard to implement, if you used an adder to add 1 to whichever address read_data_2 is set to, you'll always get the next register.
  //   FS: Yes exactly! This way we don't need additional register addresses encoded in the instruction, but we still get the benefit of combining two registers into one 16 bit word. And as another bonus, doing just another register read with that port will make it a lot easier to handle 16 bit reads with register renaming or out of order execution later. 😊
  //   JF: One thing I did notice is that random register ports lighting up as the program ran through. I'm guessing that's a result of the double pumped memory output?
  //   FS: Yeah exactly. Since the double-pumping updates the two instruction halves in different parts of the clock cycle, you get these intermittent flashes. This will go away once instruction fetching becomes properly pipelined, or we switch to a 16 bit memory bus.
endmodule
