// Digital circuit immediate.dig as structural Verilog
module immediate (
  input  [7:0] IMM_IN,
  input  IS_IMM,
  output [7:0] IMM_OUT
);

  wire _7414_1_pin8;

  PowerSupply powersupply_1 (.VDD(1'b1), .GND(1'b0));
  _7414 _7414_1 (
    .pin1(1'b0), .pin3(1'b0), .pin5(1'b0), .pin7(1'b0), .pin8(_7414_1_pin8), .pin9(IS_IMM), .pin11(1'b0),
    .pin13(1'b0), .pin14(1'b1));  // open: pin2, pin4, pin6, pin10, pin12
  _74245 _74245_1 (
    .pin1(1'b1), .pin2(IMM_IN[7]), .pin3(IMM_IN[6]), .pin4(IMM_IN[5]), .pin5(IMM_IN[4]), .pin6(IMM_IN[3]),
    .pin7(IMM_IN[2]), .pin8(IMM_IN[1]), .pin9(IMM_IN[0]), .pin10(1'b0), .pin11(IMM_OUT[0]),
    .pin12(IMM_OUT[1]), .pin13(IMM_OUT[2]), .pin14(IMM_OUT[3]), .pin15(IMM_OUT[4]), .pin16(IMM_OUT[5]),
    .pin17(IMM_OUT[6]), .pin18(IMM_OUT[7]), .pin19(_7414_1_pin8), .pin20(1'b1));
endmodule
