// Digital circuit program counter 2 - DEBUG.dig as structural Verilog
module program_counter_2___DEBUG (
  input  STEPSIZE_1,
  input  STEPSIZE_0,
  input  SEL_1,
  input  SEL_0,
  input  nENABLE,
  input  nRESET,
  input  CLK,
  input  [15:0] ABSADDR,
  input  [15:0] RELBASE,
  input  [7:0] RELOFFSET,
  output [15:0] PC,
  output nCLK,
  output [15:0] STEPADDR
);

  wire _7400_1_pin3, nMUXEN, nREGEN, PCNEXT_0, PCNEXT_1, PCNEXT_2, PCNEXT_3, PCNEXT_4, PCNEXT_5, PCNEXT_6,
       PCNEXT_7, PCNEXT_8, PCNEXT_9, PCNEXT_10, PCNEXT_11, PCNEXT_12, PCNEXT_13, PCNEXT_14, PCNEXT_15,
       RELADDR_0, RELADDR_1, RELADDR_2, RELADDR_3, RELADDR_4, RELADDR_5, RELADDR_6, RELADDR_7, RELADDR_8,
       RELADDR_9, RELADDR_10, RELADDR_11, RELADDR_12, RELADDR_13, RELADDR_14, RELADDR_15, U13_pin7, U14_pin7,
       U15_pin7, U17_pin7, U18_pin7, U19_pin7;

  _74153 U10 (
    .pin1(nMUXEN), .pin2(SEL_1), .pin3(1'b0), .pin4(ABSADDR[14]), .pin5(RELADDR_14), .pin6(STEPADDR[14]),
    .pin7(PCNEXT_14), .pin8(1'b0), .pin9(PCNEXT_15), .pin10(STEPADDR[15]), .pin11(RELADDR_15),
    .pin12(ABSADDR[15]), .pin13(1'b0), .pin14(SEL_0), .pin15(nMUXEN), .pin16(1'b1));
  _74153 U6 (
    .pin1(nMUXEN), .pin2(SEL_1), .pin3(1'b0), .pin4(ABSADDR[6]), .pin5(RELADDR_6), .pin6(STEPADDR[6]),
    .pin7(PCNEXT_6), .pin8(1'b0), .pin9(PCNEXT_7), .pin10(STEPADDR[7]), .pin11(RELADDR_7),
    .pin12(ABSADDR[7]), .pin13(1'b0), .pin14(SEL_0), .pin15(nMUXEN), .pin16(1'b1));
  PowerSupply powersupply_1 (.VDD(1'b1), .GND(1'b0));
  _74153 U9 (
    .pin1(nMUXEN), .pin2(SEL_1), .pin3(1'b0), .pin4(ABSADDR[12]), .pin5(RELADDR_12), .pin6(STEPADDR[12]),
    .pin7(PCNEXT_12), .pin8(1'b0), .pin9(PCNEXT_13), .pin10(STEPADDR[13]), .pin11(RELADDR_13),
    .pin12(ABSADDR[13]), .pin13(1'b0), .pin14(SEL_0), .pin15(nMUXEN), .pin16(1'b1));
  _74153 U5 (
    .pin1(nMUXEN), .pin2(SEL_1), .pin3(1'b0), .pin4(ABSADDR[4]), .pin5(RELADDR_4), .pin6(STEPADDR[4]),
    .pin7(PCNEXT_4), .pin8(1'b0), .pin9(PCNEXT_5), .pin10(STEPADDR[5]), .pin11(RELADDR_5),
    .pin12(ABSADDR[5]), .pin13(1'b0), .pin14(SEL_0), .pin15(nMUXEN), .pin16(1'b1));
  _74153 U8 (
    .pin1(nMUXEN), .pin2(SEL_1), .pin3(1'b0), .pin4(ABSADDR[10]), .pin5(RELADDR_10), .pin6(STEPADDR[10]),
    .pin7(PCNEXT_10), .pin8(1'b0), .pin9(PCNEXT_11), .pin10(STEPADDR[11]), .pin11(RELADDR_11),
    .pin12(ABSADDR[11]), .pin13(1'b0), .pin14(SEL_0), .pin15(nMUXEN), .pin16(1'b1));
  _74153 U4 (
    .pin1(nMUXEN), .pin2(SEL_1), .pin3(1'b0), .pin4(ABSADDR[2]), .pin5(RELADDR_2), .pin6(STEPADDR[2]),
    .pin7(PCNEXT_2), .pin8(1'b0), .pin9(PCNEXT_3), .pin10(STEPADDR[3]), .pin11(RELADDR_3),
    .pin12(ABSADDR[3]), .pin13(1'b0), .pin14(SEL_0), .pin15(nMUXEN), .pin16(1'b1));
  _7400 _7400_1 (
    .pin1(nRESET), .pin2(nENABLE), .pin3(_7400_1_pin3), .pin4(_7400_1_pin3), .pin5(_7400_1_pin3),
    .pin6(nREGEN), .pin7(1'b0), .pin8(nCLK), .pin9(CLK), .pin10(CLK), .pin11(nMUXEN), .pin12(nRESET),
    .pin13(nRESET), .pin14(1'b1));
  _74153 U7 (
    .pin1(nMUXEN), .pin2(SEL_1), .pin3(1'b0), .pin4(ABSADDR[8]), .pin5(RELADDR_8), .pin6(STEPADDR[8]),
    .pin7(PCNEXT_8), .pin8(1'b0), .pin9(PCNEXT_9), .pin10(STEPADDR[9]), .pin11(RELADDR_9),
    .pin12(ABSADDR[9]), .pin13(1'b0), .pin14(SEL_0), .pin15(nMUXEN), .pin16(1'b1));
  _74153 U3 (
    .pin1(nMUXEN), .pin2(SEL_1), .pin3(1'b0), .pin4(ABSADDR[0]), .pin5(RELADDR_0), .pin6(STEPADDR[0]),
    .pin7(PCNEXT_0), .pin8(1'b0), .pin9(PCNEXT_1), .pin10(STEPADDR[1]), .pin11(RELADDR_1),
    .pin12(ABSADDR[1]), .pin13(1'b0), .pin14(SEL_0), .pin15(nMUXEN), .pin16(1'b1));
  _74377 U2 (
    .pin1(nREGEN), .pin2(PC[15]), .pin3(PCNEXT_15), .pin4(PCNEXT_13), .pin5(PC[13]), .pin6(PC[11]),
    .pin7(PCNEXT_11), .pin8(PCNEXT_9), .pin9(PC[9]), .pin10(1'b0), .pin11(CLK), .pin12(PC[8]),
    .pin13(PCNEXT_8), .pin14(PCNEXT_10), .pin15(PC[10]), .pin16(PC[12]), .pin17(PCNEXT_12),
    .pin18(PCNEXT_14), .pin19(PC[14]), .pin20(1'b1));
  _74283 U15 (
    .pin1(STEPADDR[13]), .pin2(1'b0), .pin3(PC[13]), .pin4(STEPADDR[12]), .pin5(PC[12]), .pin6(1'b0),
    .pin7(U15_pin7), .pin8(1'b0), .pin10(STEPADDR[15]), .pin11(1'b0), .pin12(PC[15]), .pin13(STEPADDR[14]),
    .pin14(PC[14]), .pin15(1'b0), .pin16(1'b1));  // open: pin9
  _74283 U19 (
    .pin1(RELADDR_13), .pin2(RELOFFSET[7]), .pin3(RELBASE[13]), .pin4(RELADDR_12), .pin5(RELBASE[12]),
    .pin6(RELOFFSET[7]), .pin7(U19_pin7), .pin8(1'b0), .pin10(RELADDR_15), .pin11(RELOFFSET[7]),
    .pin12(RELBASE[15]), .pin13(RELADDR_14), .pin14(RELBASE[14]), .pin15(RELOFFSET[7]), .pin16(1'b1));  // open: pin9
  _74283 U14 (
    .pin1(STEPADDR[9]), .pin2(1'b0), .pin3(PC[9]), .pin4(STEPADDR[8]), .pin5(PC[8]), .pin6(1'b0),
    .pin7(U14_pin7), .pin8(1'b0), .pin9(U15_pin7), .pin10(STEPADDR[11]), .pin11(1'b0), .pin12(PC[11]),
    .pin13(STEPADDR[10]), .pin14(PC[10]), .pin15(1'b0), .pin16(1'b1));
  _74283 U18 (
    .pin1(RELADDR_9), .pin2(RELOFFSET[7]), .pin3(RELBASE[9]), .pin4(RELADDR_8), .pin5(RELBASE[8]),
    .pin6(RELOFFSET[7]), .pin7(U18_pin7), .pin8(1'b0), .pin9(U19_pin7), .pin10(RELADDR_11),
    .pin11(RELOFFSET[7]), .pin12(RELBASE[11]), .pin13(RELADDR_10), .pin14(RELBASE[10]), .pin15(RELOFFSET[7]),
    .pin16(1'b1));
  _74377 U1 (
    .pin1(nREGEN), .pin2(PC[7]), .pin3(PCNEXT_7), .pin4(PCNEXT_5), .pin5(PC[5]), .pin6(PC[3]),
    .pin7(PCNEXT_3), .pin8(PCNEXT_1), .pin9(PC[1]), .pin10(1'b0), .pin11(CLK), .pin12(PC[0]),
    .pin13(PCNEXT_0), .pin14(PCNEXT_2), .pin15(PC[2]), .pin16(PC[4]), .pin17(PCNEXT_4), .pin18(PCNEXT_6),
    .pin19(PC[6]), .pin20(1'b1));
  _74283 U13 (
    .pin1(STEPADDR[5]), .pin2(1'b0), .pin3(PC[5]), .pin4(STEPADDR[4]), .pin5(PC[4]), .pin6(1'b0),
    .pin7(U13_pin7), .pin8(1'b0), .pin9(U14_pin7), .pin10(STEPADDR[7]), .pin11(1'b0), .pin12(PC[7]),
    .pin13(STEPADDR[6]), .pin14(PC[6]), .pin15(1'b0), .pin16(1'b1));
  _74283 U17 (
    .pin1(RELADDR_5), .pin2(RELOFFSET[5]), .pin3(RELBASE[5]), .pin4(RELADDR_4), .pin5(RELBASE[4]),
    .pin6(RELOFFSET[4]), .pin7(U17_pin7), .pin8(1'b0), .pin9(U18_pin7), .pin10(RELADDR_7),
    .pin11(RELOFFSET[7]), .pin12(RELBASE[7]), .pin13(RELADDR_6), .pin14(RELBASE[6]), .pin15(RELOFFSET[6]),
    .pin16(1'b1));
  // _74283 U12: pin names not known; wires that end beside it: 1'b1, STEPADDR[1], 1'b0, STEPSIZE_1, PC[2], PC[1], STEPADDR[2], STEPADDR[0], PC[3], 1'b0, PC[0], 1'b0, STEPSIZE_0, STEPADDR[3], 1'b1, U13_pin7, 1'b0
  _74283 U16 (
    .pin1(RELADDR_1), .pin2(RELOFFSET[1]), .pin3(RELBASE[1]), .pin4(RELADDR_0), .pin5(RELBASE[0]),
    .pin6(RELOFFSET[0]), .pin7(1'b0), .pin8(1'b0), .pin9(U17_pin7), .pin10(RELADDR_3), .pin11(RELOFFSET[3]),
    .pin12(RELBASE[3]), .pin13(RELADDR_2), .pin14(RELBASE[2]), .pin15(RELOFFSET[2]), .pin16(1'b1));

  // Other names for the same wires on the sheet: ABSADDR_0 = ABSADDR[0]; ABSADDR_1 = ABSADDR[1];
  //   ABSADDR_2 = ABSADDR[2]; ABSADDR_3 = ABSADDR[3]; ABSADDR_4 = ABSADDR[4]; ABSADDR_5 = ABSADDR[5];
  //   ABSADDR_6 = ABSADDR[6]; ABSADDR_7 = ABSADDR[7]; ABSADDR_8 = ABSADDR[8]; ABSADDR_9 = ABSADDR[9];
  //   ABSADDR_10 = ABSADDR[10]; ABSADDR_11 = ABSADDR[11]; ABSADDR_12 = ABSADDR[12]; ABSADDR_13 = ABSADDR[13];
  //   ABSADDR_14 = ABSADDR[14]; ABSADDR_15 = ABSADDR[15]; PC_0 = PC[0]; PC_1 = PC[1]; PC_2 = PC[2]; PC_3 = PC[3];
  //   PC_4 = PC[4]; PC_5 = PC[5]; PC_6 = PC[6]; PC_7 = PC[7]; PC_8 = PC[8]; PC_9 = PC[9]; PC_10 = PC[10];
  //   PC_11 = PC[11]; PC_12 = PC[12]; PC_13 = PC[13]; PC_14 = PC[14]; PC_15 = PC[15]; RELBASE_0 = RELBASE[0];
  //   RELBASE_1 = RELBASE[1]; RELBASE_2 = RELBASE[2]; RELBASE_3 = RELBASE[3]; RELBASE_4 = RELBASE[4];
  //   RELBASE_5 = RELBASE[5]; RELBASE_6 = RELBASE[6]; RELBASE_7 = RELBASE[7]; RELBASE_8 = RELBASE[8];
  //   RELBASE_9 = RELBASE[9]; RELBASE_10 = RELBASE[10]; RELBASE_11 = RELBASE[11]; RELBASE_12 = RELBASE[12];
  //   RELBASE_13 = RELBASE[13]; RELBASE_14 = RELBASE[14]; RELBASE_15 = RELBASE[15]; RELOFFSET_0 = RELOFFSET[0];
  //   RELOFFSET_1 = RELOFFSET[1]; RELOFFSET_2 = RELOFFSET[2]; RELOFFSET_3 = RELOFFSET[3]; RELOFFSET_4 = RELOFFSET[4];
  //   RELOFFSET_5 = RELOFFSET[5]; RELOFFSET_6 = RELOFFSET[6]; RELOFFSET_7 = RELOFFSET[7]; STEPADDR_0 = STEPADDR[0];
  //   STEPADDR_1 = STEPADDR[1]; STEPADDR_2 = STEPADDR[2]; STEPADDR_3 = STEPADDR[3]; STEPADDR_4 = STEPADDR[4];
  //   STEPADDR_5 = STEPADDR[5]; STEPADDR_6 = STEPADDR[6]; STEPADDR_7 = STEPADDR[7]; STEPADDR_8 = STEPADDR[8];
  //   STEPADDR_9 = STEPADDR[9]; STEPADDR_10 = STEPADDR[10]; STEPADDR_11 = STEPADDR[11]; STEPADDR_12 = STEPADDR[12];
  //   STEPADDR_13 = STEPADDR[13]; STEPADDR_14 = STEPADDR[14]; STEPADDR_15 = STEPADDR[15]

  // Notes on the sheet:
  //   ABSADDR: default 255
endmodule
