// Digital circuit program memory.dig as structural Verilog
module program_memory (
  input  nCLK,
  input  CLK,
  input  nRESET,
  input  RESET,
  input  [7:0] A0,
  output [15:0] PM
);

  PowerSupply powersupply_1 (.VDD(1'b1), .GND(1'b0));
  _74273 _74273_1 (
    .pin1(nRESET), .pin2(PM[8]), .pin3(PM[0]), .pin4(PM[1]), .pin5(PM[9]), .pin6(PM[10]), .pin7(PM[2]),
    .pin8(PM[3]), .pin9(PM[11]), .pin10(1'b0), .pin11(nCLK), .pin12(PM[12]), .pin13(PM[4]), .pin14(PM[5]),
    .pin15(PM[13]), .pin16(PM[14]), .pin17(PM[6]), .pin18(PM[7]), .pin19(PM[15]), .pin20(1'b1));
  eeprom eeprom_1 (
    .nCE(1'b0), .nOE(RESET), .nWE(1'b1), .VCC(1'b1), .GND(1'b0), .I_O0(PM[0]), .I_O1(PM[1]), .I_O2(PM[2]),
    .I_O3(PM[3]), .I_O4(PM[4]), .I_O5(PM[5]), .I_O6(PM[6]), .I_O7(PM[7]), .A0(CLK), .A1(A0[1]), .A2(A0[2]),
    .A3(A0[3]), .A4(A0[4]), .A5(A0[5]), .A6(A0[6]), .A7(A0[7]), .A8(1'b0), .A9(1'b0), .A10(1'b0), .A11(1'b0),
    .A12(1'b0), .A13(1'b0), .A14(1'b0), .A15(1'b0));

  // Other names for the same wires on the sheet: Q0 = A0[0]; Q1 = A0[1]; Q2 = A0[2]; Q3 = A0[3]; Q4 = A0[4];
  //   Q5 = A0[5]; Q6 = A0[6]; Q7 = A0[7]
endmodule
