// Digital circuit register file 2.dig as structural Verilog
module register_file_2 (
  input  [3:0] WA_ADDR,
  input  [3:0] RB_ADDR,
  input  CLK,
  input  IS_IMM,
  input  [7:0] IMM,
  input  [7:0] WA,
  output [7:0] RA,
  output [7:0] RB,
  output [7:0] RC,
  output [7:0] R_1,
  output [7:0] R_2,
  output [7:0] R_3,
  output [7:0] R_4,
  output [7:0] R_5,
  output [7:0] R_6,
  output [7:0] R_7
);

  wire [7:0] register_file_controller_2_1_nra_en, register_file_controller_2_1_nrb_en,
       register_file_controller_2_1_nrc_en, register_file_controller_2_1_nwa_en;

  register_file_controller_2 register_file_controller_2_1 (
    .WA_ADDR(WA_ADDR), .RB_ADDR(RB_ADDR), .IS_IMM(IS_IMM), .nWA_EN(register_file_controller_2_1_nwa_en),
    .nRA_EN(register_file_controller_2_1_nra_en), .nRB_EN(register_file_controller_2_1_nrb_en),
    .nRC_EN(register_file_controller_2_1_nrc_en));
  register _1 (
    .CLK(CLK), .WA(IMM), .nRA_ENABLE(register_file_controller_2_1_nra_en[1]),
    .nRB_ENABLE(register_file_controller_2_1_nrb_en[1]), .nRC_ENABLE(register_file_controller_2_1_nrc_en[1]),
    .nWA_ENABLE(register_file_controller_2_1_nwa_en[1]), .REG(R_1), .RA(RA), .RB(IMM), .RC(RC));
  register _2 (
    .CLK(CLK), .WA(IMM), .nRA_ENABLE(register_file_controller_2_1_nra_en[2]),
    .nRB_ENABLE(register_file_controller_2_1_nrb_en[2]), .nRC_ENABLE(register_file_controller_2_1_nrc_en[2]),
    .nWA_ENABLE(register_file_controller_2_1_nwa_en[2]), .REG(R_2), .RA(RA), .RB(IMM), .RC(RC));
  register _3 (
    .CLK(CLK), .WA(IMM), .nRA_ENABLE(register_file_controller_2_1_nra_en[3]),
    .nRB_ENABLE(register_file_controller_2_1_nrb_en[3]), .nRC_ENABLE(register_file_controller_2_1_nrc_en[3]),
    .nWA_ENABLE(register_file_controller_2_1_nwa_en[3]), .REG(R_3), .RA(RA), .RB(IMM), .RC(RC));
  register _4 (
    .CLK(CLK), .WA(IMM), .nRA_ENABLE(register_file_controller_2_1_nra_en[4]),
    .nRB_ENABLE(register_file_controller_2_1_nrb_en[4]), .nRC_ENABLE(register_file_controller_2_1_nrc_en[4]),
    .nWA_ENABLE(register_file_controller_2_1_nwa_en[4]), .REG(R_4), .RA(RA), .RB(IMM), .RC(RC));
  register _5 (
    .CLK(CLK), .WA(IMM), .nRA_ENABLE(register_file_controller_2_1_nra_en[5]),
    .nRB_ENABLE(register_file_controller_2_1_nrb_en[5]), .nRC_ENABLE(register_file_controller_2_1_nrc_en[5]),
    .nWA_ENABLE(register_file_controller_2_1_nwa_en[5]), .REG(R_5), .RA(RA), .RB(IMM), .RC(RC));
  register _6 (
    .CLK(CLK), .WA(IMM), .nRA_ENABLE(register_file_controller_2_1_nra_en[6]),
    .nRB_ENABLE(register_file_controller_2_1_nrb_en[6]), .nRC_ENABLE(register_file_controller_2_1_nrc_en[6]),
    .nWA_ENABLE(register_file_controller_2_1_nwa_en[6]), .REG(R_6), .RA(RA), .RB(IMM), .RC(RC));
  register _7 (
    .CLK(CLK), .WA(IMM), .nRA_ENABLE(register_file_controller_2_1_nra_en[7]),
    .nRB_ENABLE(register_file_controller_2_1_nrb_en[7]), .nRC_ENABLE(register_file_controller_2_1_nrc_en[7]),
    .nWA_ENABLE(register_file_controller_2_1_nwa_en[7]), .REG(R_7), .RA(RA), .RB(IMM), .RC(RC));

  assign RB = IMM;
  assign WA = IMM;
endmodule
