// Digital circuit register file controller 2.dig as structural Verilog
module register_file_controller_2 (
  input  [3:0] WA_ADDR,
  input  [3:0] RB_ADDR,
  input  IS_IMM,
  output [7:0] nWA_EN,
  output [7:0] nRA_EN,
  output [7:0] nRB_EN,
  output [7:0] nRC_EN
);

  PowerSupply powersupply_1 (.VDD(1'b1), .GND(1'b0));
  _74138 _74138_1 (
    .pin1(WA_ADDR[0]), .pin2(WA_ADDR[1]), .pin3(WA_ADDR[2]), .pin4(1'b0), .pin5(1'b0), .pin6(1'b1),
    .pin7(nWA_EN[7]), .pin8(1'b0), .pin9(nWA_EN[6]), .pin10(nWA_EN[5]), .pin11(nWA_EN[4]), .pin12(nWA_EN[3]),
    .pin13(nWA_EN[2]), .pin14(nWA_EN[1]), .pin15(nWA_EN[0]), .pin16(1'b1));
  _74138 _74138_2 (
    .pin1(WA_ADDR[0]), .pin2(WA_ADDR[1]), .pin3(WA_ADDR[2]), .pin4(1'b0), .pin5(1'b0), .pin6(1'b1),
    .pin7(nRA_EN[7]), .pin8(1'b0), .pin9(nRA_EN[6]), .pin10(nRA_EN[5]), .pin11(nRA_EN[4]), .pin12(nRA_EN[3]),
    .pin13(nRA_EN[2]), .pin14(nRA_EN[1]), .pin15(nRA_EN[0]), .pin16(1'b1));
  _74138 _74138_3 (
    .pin1(RB_ADDR[0]), .pin2(RB_ADDR[1]), .pin3(RB_ADDR[2]), .pin4(IS_IMM), .pin5(1'b0), .pin6(1'b1),
    .pin7(nRB_EN[7]), .pin8(1'b0), .pin9(nRB_EN[6]), .pin10(nRB_EN[5]), .pin11(nRB_EN[4]), .pin12(nRB_EN[3]),
    .pin13(nRB_EN[2]), .pin14(nRB_EN[1]), .pin15(nRB_EN[0]), .pin16(1'b1));

  assign nRC_EN = {nRB_EN[7], nRB_EN[5:0], 1'b1};

  // Other names for the same wires on the sheet: PM3 = IS_IMM
endmodule
